// Digital circuit alu_16.dig as structural Verilog
module alu_16 (
  input  [15:0] A,
  input  [15:0] B,
  input  [3:0] OP,
  output [15:0] RES
);

  wire [0:0] comparator_1_eq, comparator_1_gt;
  wire [15:0] add_1_s, and_1_out, barrelshifter_1_out, barrelshifter_2_out, barrelshifter_3_out,
       barrelshifter_4_out, div_1_q, mul_1_mul, neg_1_out, not_1_out, or_1_out, sub_1_s, xor_1_out;
  wire [31:16] mul_1_mul_2;

  Add #(.Bits(16)) add_1 (.a(A), .b(B), .c_i(1'b0), .s(add_1_s));  // open: c_o
  Sub #(.Bits(16)) sub_1 (.a(A), .b(B), .c_i(1'b0), .s(sub_1_s));  // open: c_o
  Mul #(.Bits(16)) mul_1 (.a(A), .b(B), .mul({mul_1_mul_2, mul_1_mul}));
  Div #(.Bits(16)) div_1 (.a(A), .b(B), .q(div_1_q));  // open: r
  assign and_1_out = A & B;  // And and_1, 16 bits wide
  assign or_1_out = A | B;  // Or or_1, 16 bits wide
  assign xor_1_out = A ^ B;  // XOr xor_1, 16 bits wide
  assign not_1_out = ~A;  // Not not_1, 16 bits wide
  BarrelShifter #(.Bits(16)) barrelshifter_1 (.in(A), .shift(5'b00001), .out(barrelshifter_1_out));
  BarrelShifter #(.Bits(16)) barrelshifter_2 (.in(A), .shift(B[4:0]), .out(barrelshifter_2_out));
  BarrelShifter #(.Bits(16)) barrelshifter_3 (.in(A), .shift(5'b00001), .out(barrelshifter_3_out));
  BarrelShifter #(.Bits(16)) barrelshifter_4 (.in(A), .shift(B[4:0]), .out(barrelshifter_4_out));
  Neg #(.Bits(16)) neg_1 (.in(B), .out(neg_1_out));
  Comparator #(.Bits(16)) comparator_1 (.a(A), .b(B), .gt(comparator_1_gt[0]), .eq(comparator_1_eq[0]));  // open: lt
  Multiplexer #(.Selector_Bits(4), .Bits(16)) multiplexer_1 (
    .sel(OP), .in_0(add_1_s), .in_1(sub_1_s), .in_2(mul_1_mul), .in_3(div_1_q), .in_4(and_1_out),
    .in_5(or_1_out), .in_6(xor_1_out), .in_7(not_1_out), .in_8(barrelshifter_1_out),
    .in_9(barrelshifter_2_out), .in_10(barrelshifter_3_out), .in_11(barrelshifter_4_out), .in_12(neg_1_out),
    .in_13({{15{1'b0}}, comparator_1_gt[0]}), .in_14({{15{1'b0}}, comparator_1_eq[0]}), .in_15(B), .out(RES));
endmodule
