// Digital circuit alu_8.dig as structural Verilog
module alu_8 (
  input  [7:0] A,
  input  [7:0] B,
  input  [3:0] OP,
  output [7:0] RES,
  output [7:0] C
);

  wire [0:0] add_1_c_o, comparator_1_eq, comparator_1_gt, sub_1_c_o;
  wire [7:0] add_1_s, and_1_out, barrelshifter_1_out, barrelshifter_2_out, barrelshifter_3_out,
       barrelshifter_4_out, div_1_q, div_1_r, mul_1_mul, mul_1_mul_2, neg_1_out, not_1_out, or_1_out,
       sub_1_s, xor_1_out;

  Add #(.Bits(8)) add_1 (.a(A), .b(B), .c_i(1'b0), .s(add_1_s), .c_o(add_1_c_o[0]));
  Sub #(.Bits(8)) sub_1 (.a(A), .b(B), .c_i(1'b0), .s(sub_1_s), .c_o(sub_1_c_o[0]));
  Mul #(.Bits(8)) mul_1 (.a(A), .b(B), .mul({mul_1_mul_2, mul_1_mul}));
  Div #(.Bits(8)) div_1 (.a(A), .b(B), .q(div_1_q), .r(div_1_r));
  assign and_1_out = A & B;  // And and_1, 8 bits wide
  assign or_1_out = A | B;  // Or or_1, 8 bits wide
  assign xor_1_out = A ^ B;  // XOr xor_1, 8 bits wide
  assign not_1_out = ~A;  // Not not_1, 8 bits wide
  BarrelShifter #(.Bits(8)) barrelshifter_1 (.in(A), .shift(4'b0001), .out(barrelshifter_1_out));
  BarrelShifter #(.Bits(8)) barrelshifter_2 (.in(A), .shift(B[3:0]), .out(barrelshifter_2_out));
  BarrelShifter #(.Bits(8)) barrelshifter_3 (.in(A), .shift(4'b0001), .out(barrelshifter_3_out));
  BarrelShifter #(.Bits(8)) barrelshifter_4 (.in(A), .shift(B[3:0]), .out(barrelshifter_4_out));
  Neg #(.Bits(8)) neg_1 (.in(B), .out(neg_1_out));
  Comparator #(.Bits(8)) comparator_1 (.a(A), .b(B), .gt(comparator_1_gt[0]), .eq(comparator_1_eq[0]));  // open: lt
  Multiplexer #(.Selector_Bits(4), .Bits(8)) multiplexer_1 (
    .sel(OP), .in_0(add_1_s), .in_1(sub_1_s), .in_2(mul_1_mul), .in_3(div_1_q), .in_4(and_1_out),
    .in_5(or_1_out), .in_6(xor_1_out), .in_7(not_1_out), .in_8(barrelshifter_1_out),
    .in_9(barrelshifter_2_out), .in_10(barrelshifter_3_out), .in_11(barrelshifter_4_out), .in_12(neg_1_out),
    .in_13({{7{1'b0}}, comparator_1_gt[0]}), .in_14({{7{1'b0}}, comparator_1_eq[0]}), .in_15(B), .out(RES));
  Multiplexer #(.Selector_Bits(2), .Bits(8)) multiplexer_2 (
    .sel(OP[1:0]), .in_0({{7{1'b0}}, add_1_c_o[0]}), .in_1({{7{1'b0}}, sub_1_c_o[0]}), .in_2(mul_1_mul_2),
    .in_3(div_1_r), .out(C));
endmodule
