// Digital circuit register_file.dig as structural Verilog
module register_file (
  input  [7:0] D_IN,
  input  CLK,
  input  W_A,
  input  W_D,
  input  [7:0] A_IN,
  output [7:0] D_OUT
);

  wire [7:0] REGF_ADDR_q;

  Register #(.Bits(8)) REGF_ADDR (.D(A_IN), .C(CLK), .en(W_A), .Q(REGF_ADDR_q));
  BlockRAMDualPort #(.AddrBits(8), .Bits(8)) REGF_MEM (.A(REGF_ADDR_q), .Din(D_IN), .str(W_D), .C(CLK), .D(D_OUT));

  // Notes on the sheet:
  //   D_IN: Data input
  //   A_IN: Address input
endmodule
