// Digital circuit sreg_21.dig as structural Verilog
module sreg_21 (
  input  [6:0] IN,
  input  CLK,
  input  ENA,
  output [20:0] OUT
);

  Register #(.Bits(21)) register_1 (.D({OUT[13:0], IN}), .C(CLK), .en(ENA), .Q(OUT));
endmodule
