// Digital circuit stack.dig as structural Verilog
module stack (
  input  PUSH,
  input  CLK,
  input  POP,
  input  SP_WRITE,
  input  TOS_WRITE,
  input  [7:0] SP_IN,
  input  [7:0] TOS_IN,
  output [7:0] TOS_OUT,
  output [7:0] SP_OUT
);

  wire or_1_out;

  or or_1 (or_1_out, PUSH, POP);
  CounterPreset #(.Bits(8)) STACK_SP (
    .en(or_1_out), .C(CLK), .dir(POP), .in(SP_IN), .ld(SP_WRITE), .clr(1'b0), .out(SP_OUT));  // open: ovf
  BlockRAMDualPort #(.AddrBits(8), .Bits(8)) STACK_MEM (
    .A(SP_OUT), .Din(TOS_IN), .str(TOS_WRITE), .C(CLK), .D(TOS_OUT));
endmodule
