// Digital circuit t3lc_huge.dig as structural Verilog
module t3lc_huge (
  input  CLK,
  input  [7:0] IROM_IN,
  input  [7:0] EXT_IN,
  input  INTR,
  output [7:0] EXT_OUT,
  output HALTED,
  output [5:0] EXT_SEL,
  output [23:0] IROM_ADDR,
  output [23:0] EXT_ADDR,
  output EXT_READ,
  output EXT_WRITE
);

  wire ALU8_CARRY_READ, ALU8_RES_READ, ALU16_HI_READ, ALU16_LATCH, ALU16_LO_READ, and_2_out, and_4_out,
       and_5_out, and_6_out, and_7_out, BRANCH_A_EQZ, BRANCH_A_NEZ, BRANCH_B_EQZ, BRANCH_B_NEZ,
       comparator_1_eq, comparator_2_eq, EXT_PAGE_READ, EXT_PAGE_WRITE, HALT, HALT_q, IMM_OP_READ,
       IROM_PAGE_READ, JUMP, JUMP_CTRL_WRITE, OP_READ, OP_SPECIAl0, OP_SPECIAL1, OP_WRITE, or_1_out,
       or_2_out, RAM_SEL_WRITE, REGF_A_ADDR_WRITE, REGF_A_MEM_WRITE, REGF_A_READ, REGF_B_ADDR_WRITE,
       REGF_B_MEM_WRITE, REGF_B_READ, REGF_I_ADDR_WRITE, REGF_I_MEM_WRITE, REGF_I_READ, REGF_J_ADDR_WRITE,
       REGF_J_MEM_WRITE, REGF_J_READ, ROM_PAGE_WRITE, SREG_IMM7_READ, SREG_IMM8_READ, SREG_IMM14_HI_READ,
       SREG_IMM16_HI_READ, STACK_X_POP, STACK_X_PUSH, STACK_X_SP_READ, STACK_X_SP_WRITE, STACK_X_TOS_READ,
       STACK_X_TOS_WRITE, STACK_Y_POP, STACK_Y_PUSH, STACK_Y_SP_READ, STACK_Y_SP_WRITE, STACK_Y_TOS_READ,
       STACK_Y_TOS_WRITE;
  wire [1:0] multiplexer_5_out, REG_EXT_q, REG_JUMP_CTRL_q;
  wire [6:0] SREG_IMM7;
  wire [7:0] ALU_8_c, ALU_8_res, driver_1_out, IMM_OP_VALUE, multiplexer_1_out, multiplexer_3_out,
       pulldown_2_out, REG_DATA_q, REGF_A, REGF_I, register_1_q, register_1_q_2, STACK_X, STACK_X_sp_out,
       STACK_Y_sp_out;
  wire [7:6] SREG_IMM16_HI;
  wire [7:7] SREG_IMM8;
  wire [10:5] REG_JUMP_CTRL_q_2;
  wire [13:8] SREG_IMM14;
  wire [15:0] alu_16_1_res, EXT_ADDR_t, LOAD_PC_ADDR, multiplexer_2_out, multiplexer_4_out;
  wire [15:8] REGF_AB, REGF_IJ, STACK_XY;
  wire [20:16] SREG_IMM_21;
  wire [23:15] driver_20_out;
  wire [23:16] EXT_PAGE_q;
  wire [31:0] decoder_1_out_0, decoder_2_out_0, decoder_3_out_0, decoder_4_out_0, driver_22_out;
  wire [31:3] driver_21_out;
  wire [31:17] driver_19_out;

  sreg_21 sreg_21_1 (
    .IN(IROM_IN[6:0]), .CLK(CLK), .ENA(IROM_IN[7]),
    .OUT({SREG_IMM_21, SREG_IMM16_HI, SREG_IMM14, SREG_IMM8[7], SREG_IMM7}));
  assign driver_1_out = EXT_READ ? EXT_IN : 8'bz;  // Driver driver_1
  Register #(.Bits(8)) REG_DATA (.D(driver_1_out), .C(CLK), .en(OP_READ), .Q(REG_DATA_q));
  Register #(.Bits(8)) IROM_PAGE (.D(REG_DATA_q), .C(CLK), .en(ROM_PAGE_WRITE), .Q(IROM_ADDR[23:16]));
  Register #(.Bits(8)) EXT_PAGE (.D(REG_DATA_q), .C(CLK), .en(EXT_PAGE_WRITE), .Q(EXT_PAGE_q));
  register_file u_REGF_A (
    .D_IN(REG_DATA_q), .CLK(CLK), .W_A(REGF_A_ADDR_WRITE), .W_D(REGF_A_MEM_WRITE), .A_IN(REG_DATA_q),
    .D_OUT(REGF_A));
  register_file REGF_B (
    .D_IN(REG_DATA_q), .CLK(CLK), .W_A(REGF_B_ADDR_WRITE), .W_D(REGF_B_MEM_WRITE), .A_IN(REG_DATA_q),
    .D_OUT(REGF_AB));
  register_file u_REGF_I (
    .D_IN(REG_DATA_q), .CLK(CLK), .W_A(REGF_I_ADDR_WRITE), .W_D(REGF_I_MEM_WRITE), .A_IN(REG_DATA_q),
    .D_OUT(REGF_I));
  register_file REGF_J (
    .D_IN(REG_DATA_q), .CLK(CLK), .W_A(REGF_J_ADDR_WRITE), .W_D(REGF_J_MEM_WRITE), .A_IN(REG_DATA_q),
    .D_OUT(REGF_IJ));
  stack u_STACK_X (
    .PUSH(STACK_X_PUSH), .CLK(CLK), .POP(STACK_X_POP), .SP_WRITE(STACK_X_SP_WRITE),
    .TOS_WRITE(STACK_X_TOS_WRITE), .SP_IN(REG_DATA_q), .TOS_IN(REG_DATA_q), .TOS_OUT(STACK_X),
    .SP_OUT(STACK_X_sp_out));
  stack STACK_Y (
    .PUSH(STACK_Y_PUSH), .CLK(CLK), .POP(STACK_Y_POP), .SP_WRITE(STACK_Y_SP_WRITE),
    .TOS_WRITE(STACK_Y_TOS_WRITE), .SP_IN(REG_DATA_q), .TOS_IN(REG_DATA_q), .TOS_OUT(STACK_XY),
    .SP_OUT(STACK_Y_sp_out));
  Multiplexer #(.Selector_Bits(3), .Bits(8)) multiplexer_1 (
    .sel(SREG_IMM7[6:4]), .in_0(REGF_A), .in_1(REGF_AB), .in_2(REGF_I), .in_3(REGF_IJ), .in_4(STACK_X),
    .in_5(STACK_XY), .in_6(8'h1), .in_7({SREG_IMM_21[17:16], SREG_IMM16_HI, SREG_IMM14[13:10]}),
    .out(multiplexer_1_out));
  Multiplexer #(.Selector_Bits(2), .Bits(16)) multiplexer_2 (
    .sel(SREG_IMM7[5:4]), .in_0({STACK_XY, STACK_X}), .in_1({REGF_IJ, REGF_I}), .in_2({REGF_AB, REGF_A}),
    .in_3(IROM_ADDR[15:0]), .out(multiplexer_2_out));
  assign EXT_OUT = EXT_WRITE ? REG_DATA_q : 8'bz;  // Driver driver_2
  Register #(.Bits(8)) REG_JUMP_CTRL (
    .D(REG_DATA_q), .C(CLK), .en(JUMP_CTRL_WRITE), .Q({REG_JUMP_CTRL_q_2, REG_JUMP_CTRL_q}));
  Register #(.Bits(8)) REG_EXT (.D(REG_DATA_q), .C(CLK), .en(JUMP_CTRL_WRITE), .Q({EXT_SEL, REG_EXT_q}));
  and and_1 (OP_WRITE, IROM_IN[5], ~IROM_IN[6], ~IROM_IN[7]);  // And
  PullDown #(.Bits(8)) pulldown_1 (.out(driver_1_out));
  or or_1 (or_1_out, EXT_READ, EXT_WRITE);
  Multiplexer #(.Selector_Bits(3), .Bits(8)) multiplexer_3 (
    .sel({SREG_IMM14[9:8], SREG_IMM8[7]}), .in_0(REGF_A), .in_1(REGF_AB), .in_2(REGF_I), .in_3(REGF_IJ),
    .in_4(STACK_X), .in_5(STACK_XY), .in_6(8'h1),
    .in_7({SREG_IMM_21[17:16], SREG_IMM16_HI, SREG_IMM14[13:10]}), .out(multiplexer_3_out));
  Multiplexer #(.Selector_Bits(2), .Bits(16)) multiplexer_4 (
    .sel({SREG_IMM14[8], SREG_IMM8[7]}), .in_0({STACK_XY, STACK_X}), .in_1({REGF_IJ, REGF_I}),
    .in_2({REGF_AB, REGF_A}), .in_3(IROM_ADDR[15:0]), .out(multiplexer_4_out));
  and and_2 (and_2_out, OP_READ, ~EXT_READ);  // And
  assign driver_1_out = and_2_out ? pulldown_2_out : 8'bz;  // Driver driver_3
  PullDown #(.Bits(8)) pulldown_2 (.out(pulldown_2_out));
  assign EXT_ADDR = or_1_out ? {EXT_PAGE_q, EXT_ADDR_t} : 24'bz;  // Driver driver_4
  alu_8 ALU_8 (.A(multiplexer_1_out), .B(multiplexer_3_out), .OP(SREG_IMM7[3:0]), .RES(ALU_8_res), .C(ALU_8_c));
  alu_16 alu_16_1 (.A(multiplexer_2_out), .B(multiplexer_4_out), .OP(SREG_IMM7[3:0]), .RES(alu_16_1_res));
  Multiplexer #(.Bits(2)) multiplexer_5 (.sel(INTR), .in_0(REG_JUMP_CTRL_q), .in_1(2'b00), .out(multiplexer_5_out));
  Multiplexer #(.Selector_Bits(2), .Bits(16)) multiplexer_6 (
    .sel(multiplexer_5_out), .in_0({{5{1'b0}}, REG_JUMP_CTRL_q_2, {5{1'b0}}}), .in_1({REGF_AB, REGF_A}),
    .in_2({REGF_IJ, REGF_I}), .in_3({STACK_XY, STACK_X}), .out(LOAD_PC_ADDR));
  Multiplexer #(.Selector_Bits(2), .Bits(16)) multiplexer_7 (
    .sel(REG_EXT_q), .in_0({SREG_IMM16_HI, SREG_IMM14, SREG_IMM8[7], SREG_IMM7}), .in_1({REGF_AB, REGF_A}),
    .in_2({REGF_IJ, REGF_I}), .in_3({STACK_XY, STACK_X}), .out(EXT_ADDR_t));
  Register #(.Bits(16)) register_1 (.D(alu_16_1_res), .C(CLK), .en(ALU16_LATCH), .Q({register_1_q_2, register_1_q}));
  assign pulldown_2_out = IROM_PAGE_READ ? IROM_ADDR[23:16] : 8'bz;  // Driver driver_5
  assign pulldown_2_out = EXT_PAGE_READ ? EXT_PAGE_q : 8'bz;  // Driver driver_6
  assign pulldown_2_out = REGF_A_READ ? REGF_A : 8'bz;  // Driver driver_7
  assign pulldown_2_out = REGF_B_READ ? REGF_AB : 8'bz;  // Driver driver_8
  assign pulldown_2_out = REGF_I_READ ? REGF_I : 8'bz;  // Driver driver_9
  assign pulldown_2_out = REGF_J_READ ? REGF_IJ : 8'bz;  // Driver driver_10
  assign pulldown_2_out = STACK_X_TOS_READ ? STACK_X : 8'bz;  // Driver driver_11
  assign pulldown_2_out = STACK_X_SP_READ ? STACK_X_sp_out : 8'bz;  // Driver driver_12
  assign pulldown_2_out = STACK_Y_TOS_READ ? STACK_XY : 8'bz;  // Driver driver_13
  assign pulldown_2_out = STACK_Y_SP_READ ? STACK_Y_sp_out : 8'bz;  // Driver driver_14
  assign pulldown_2_out = ALU8_RES_READ ? ALU_8_res : 8'bz;  // Driver driver_15
  assign pulldown_2_out = ALU8_CARRY_READ ? ALU_8_c : 8'bz;  // Driver driver_16
  assign pulldown_2_out = ALU16_LO_READ ? register_1_q : 8'bz;  // Driver driver_17
  assign pulldown_2_out = ALU16_HI_READ ? register_1_q_2 : 8'bz;  // Driver driver_18
  Decoder #(.Selector_Bits(5)) decoder_1 (
    .sel(IROM_IN[4:0]), .out_0(decoder_1_out_0[0]), .out_1(decoder_1_out_0[1]), .out_2(decoder_1_out_0[2]),
    .out_3(decoder_1_out_0[3]), .out_4(decoder_1_out_0[4]), .out_5(decoder_1_out_0[5]),
    .out_6(decoder_1_out_0[6]), .out_7(decoder_1_out_0[7]), .out_8(decoder_1_out_0[8]),
    .out_9(decoder_1_out_0[9]), .out_10(decoder_1_out_0[10]), .out_11(decoder_1_out_0[11]),
    .out_12(decoder_1_out_0[12]), .out_13(decoder_1_out_0[13]), .out_14(decoder_1_out_0[14]),
    .out_15(decoder_1_out_0[15]), .out_16(decoder_1_out_0[16]), .out_17(decoder_1_out_0[17]),
    .out_18(decoder_1_out_0[18]), .out_19(decoder_1_out_0[19]), .out_20(decoder_1_out_0[20]),
    .out_21(decoder_1_out_0[21]), .out_22(decoder_1_out_0[22]), .out_23(decoder_1_out_0[23]),
    .out_24(decoder_1_out_0[24]), .out_25(decoder_1_out_0[25]), .out_26(decoder_1_out_0[26]),
    .out_27(decoder_1_out_0[27]), .out_28(decoder_1_out_0[28]), .out_29(decoder_1_out_0[29]),
    .out_30(decoder_1_out_0[30]), .out_31(decoder_1_out_0[31]));
  assign {driver_19_out, JUMP_CTRL_WRITE, RAM_SEL_WRITE, EXT_WRITE, ROM_PAGE_WRITE, EXT_PAGE_WRITE, STACK_Y_SP_WRITE, STACK_Y_TOS_WRITE, STACK_X_SP_WRITE, STACK_X_TOS_WRITE, REGF_J_ADDR_WRITE, REGF_I_ADDR_WRITE, REGF_B_ADDR_WRITE, REGF_A_ADDR_WRITE, REGF_J_MEM_WRITE, REGF_I_MEM_WRITE, REGF_B_MEM_WRITE, REGF_A_MEM_WRITE} = OP_WRITE ? decoder_1_out_0 : 32'bz;  // Driver driver_19
  PullDown #(.Bits(32)) pulldown_3 (.out({driver_19_out, JUMP_CTRL_WRITE, RAM_SEL_WRITE, EXT_WRITE, ROM_PAGE_WRITE, EXT_PAGE_WRITE, STACK_Y_SP_WRITE, STACK_Y_TOS_WRITE, STACK_X_SP_WRITE, STACK_X_TOS_WRITE, REGF_J_ADDR_WRITE, REGF_I_ADDR_WRITE, REGF_B_ADDR_WRITE, REGF_A_ADDR_WRITE, REGF_J_MEM_WRITE, REGF_I_MEM_WRITE, REGF_B_MEM_WRITE, REGF_A_MEM_WRITE}));
  and and_3 (OP_READ, ~IROM_IN[5], IROM_IN[6], ~IROM_IN[7]);  // And
  Comparator #(.Bits(8)) comparator_1 (.a(REGF_A), .b({8{1'b0}}), .eq(comparator_1_eq));  // open: gt, lt
  Comparator #(.Bits(8)) comparator_2 (.a({8{1'b0}}), .b(REGF_AB), .eq(comparator_2_eq));  // open: gt, lt
  and and_4 (and_4_out, BRANCH_A_EQZ, comparator_1_eq);
  and and_5 (and_5_out, ~comparator_1_eq, BRANCH_A_NEZ);  // And
  and and_6 (and_6_out, BRANCH_B_EQZ, comparator_2_eq);
  and and_7 (and_7_out, ~comparator_2_eq, BRANCH_B_NEZ);  // And
  or or_2 (or_2_out, INTR, and_4_out, and_5_out, and_6_out, and_7_out, JUMP);
  D_FF u_HALT (.D(HALT), .C(CLK), .Q(HALT_q), .nQ(HALTED));
  CounterPreset #(.Bits(16)) CNT_PC (
    .en(HALT_q), .C(CLK), .dir(1'b0), .in(LOAD_PC_ADDR), .ld(or_2_out), .clr(1'b0), .out(IROM_ADDR[15:0]));  // open: ovf
  Decoder #(.Selector_Bits(5)) decoder_2 (
    .sel(IROM_IN[4:0]), .out_0(decoder_2_out_0[0]), .out_1(decoder_2_out_0[1]), .out_2(decoder_2_out_0[2]),
    .out_3(decoder_2_out_0[3]), .out_4(decoder_2_out_0[4]), .out_5(decoder_2_out_0[5]),
    .out_6(decoder_2_out_0[6]), .out_7(decoder_2_out_0[7]), .out_8(decoder_2_out_0[8]),
    .out_9(decoder_2_out_0[9]), .out_10(decoder_2_out_0[10]), .out_11(decoder_2_out_0[11]),
    .out_12(decoder_2_out_0[12]), .out_13(decoder_2_out_0[13]), .out_14(decoder_2_out_0[14]),
    .out_15(decoder_2_out_0[15]), .out_16(decoder_2_out_0[16]), .out_17(decoder_2_out_0[17]),
    .out_18(decoder_2_out_0[18]), .out_19(decoder_2_out_0[19]), .out_20(decoder_2_out_0[20]),
    .out_21(decoder_2_out_0[21]), .out_22(decoder_2_out_0[22]), .out_23(decoder_2_out_0[23]),
    .out_24(decoder_2_out_0[24]), .out_25(decoder_2_out_0[25]), .out_26(decoder_2_out_0[26]),
    .out_27(decoder_2_out_0[27]), .out_28(decoder_2_out_0[28]), .out_29(decoder_2_out_0[29]),
    .out_30(decoder_2_out_0[30]), .out_31(decoder_2_out_0[31]));
  assign {IMM_OP_VALUE[0], IMM_OP_VALUE[1], IMM_OP_VALUE[2], IMM_OP_VALUE[3], IMM_OP_VALUE[4], IMM_OP_VALUE[5], IMM_OP_VALUE[6], IMM_OP_VALUE[7], driver_20_out[23], SREG_IMM16_HI_READ, SREG_IMM14_HI_READ, SREG_IMM8_READ, SREG_IMM7_READ, driver_20_out[18:15], EXT_READ, IROM_PAGE_READ, EXT_PAGE_READ, STACK_Y_SP_READ, STACK_Y_TOS_READ, STACK_X_SP_READ, STACK_X_TOS_READ, ALU16_HI_READ, ALU16_LO_READ, ALU8_CARRY_READ, ALU8_RES_READ, REGF_J_READ, REGF_I_READ, REGF_B_READ, REGF_A_READ} = OP_READ ? decoder_2_out_0 : 32'bz;  // Driver driver_20
  PullDown #(.Bits(32)) pulldown_4 (.out({IMM_OP_VALUE[0], IMM_OP_VALUE[1], IMM_OP_VALUE[2], IMM_OP_VALUE[3], IMM_OP_VALUE[4], IMM_OP_VALUE[5], IMM_OP_VALUE[6], IMM_OP_VALUE[7], driver_20_out[23], SREG_IMM16_HI_READ, SREG_IMM14_HI_READ, SREG_IMM8_READ, SREG_IMM7_READ, driver_20_out[18:15], EXT_READ, IROM_PAGE_READ, EXT_PAGE_READ, STACK_Y_SP_READ, STACK_Y_TOS_READ, STACK_X_SP_READ, STACK_X_TOS_READ, ALU16_HI_READ, ALU16_LO_READ, ALU8_CARRY_READ, ALU8_RES_READ, REGF_J_READ, REGF_I_READ, REGF_B_READ, REGF_A_READ}));
  or or_3 (IMM_OP_READ, driver_20_out[23], IMM_OP_VALUE[7], IMM_OP_VALUE[6], IMM_OP_VALUE[5], IMM_OP_VALUE[4], IMM_OP_VALUE[3], IMM_OP_VALUE[2], IMM_OP_VALUE[1], IMM_OP_VALUE[0]);
  and and_8 (OP_SPECIAl0, ~IROM_IN[5], ~IROM_IN[6], ~IROM_IN[7]);  // And
  Decoder #(.Selector_Bits(5)) decoder_3 (
    .sel(IROM_IN[4:0]), .out_0(decoder_3_out_0[0]), .out_1(decoder_3_out_0[1]), .out_2(decoder_3_out_0[2]),
    .out_3(decoder_3_out_0[3]), .out_4(decoder_3_out_0[4]), .out_5(decoder_3_out_0[5]),
    .out_6(decoder_3_out_0[6]), .out_7(decoder_3_out_0[7]), .out_8(decoder_3_out_0[8]),
    .out_9(decoder_3_out_0[9]), .out_10(decoder_3_out_0[10]), .out_11(decoder_3_out_0[11]),
    .out_12(decoder_3_out_0[12]), .out_13(decoder_3_out_0[13]), .out_14(decoder_3_out_0[14]),
    .out_15(decoder_3_out_0[15]), .out_16(decoder_3_out_0[16]), .out_17(decoder_3_out_0[17]),
    .out_18(decoder_3_out_0[18]), .out_19(decoder_3_out_0[19]), .out_20(decoder_3_out_0[20]),
    .out_21(decoder_3_out_0[21]), .out_22(decoder_3_out_0[22]), .out_23(decoder_3_out_0[23]),
    .out_24(decoder_3_out_0[24]), .out_25(decoder_3_out_0[25]), .out_26(decoder_3_out_0[26]),
    .out_27(decoder_3_out_0[27]), .out_28(decoder_3_out_0[28]), .out_29(decoder_3_out_0[29]),
    .out_30(decoder_3_out_0[30]), .out_31(decoder_3_out_0[31]));
  assign {driver_21_out[31:12], STACK_Y_POP, STACK_Y_PUSH, STACK_X_POP, STACK_X_PUSH, BRANCH_B_NEZ, BRANCH_B_EQZ, BRANCH_A_NEZ, BRANCH_A_EQZ, driver_21_out[3], ALU16_LATCH, JUMP, HALT} = OP_SPECIAl0 ? decoder_3_out_0 : 32'bz;  // Driver driver_21
  PullDown #(.Bits(32)) pulldown_5 (.out({driver_21_out[31:12], STACK_Y_POP, STACK_Y_PUSH, STACK_X_POP, STACK_X_PUSH, BRANCH_B_NEZ, BRANCH_B_EQZ, BRANCH_A_NEZ, BRANCH_A_EQZ, driver_21_out[3], ALU16_LATCH, JUMP, HALT}));
  and and_9 (OP_SPECIAL1, IROM_IN[5], IROM_IN[6], ~IROM_IN[7]);  // And
  Decoder #(.Selector_Bits(5)) decoder_4 (
    .sel(IROM_IN[4:0]), .out_0(decoder_4_out_0[0]), .out_1(decoder_4_out_0[1]), .out_2(decoder_4_out_0[2]),
    .out_3(decoder_4_out_0[3]), .out_4(decoder_4_out_0[4]), .out_5(decoder_4_out_0[5]),
    .out_6(decoder_4_out_0[6]), .out_7(decoder_4_out_0[7]), .out_8(decoder_4_out_0[8]),
    .out_9(decoder_4_out_0[9]), .out_10(decoder_4_out_0[10]), .out_11(decoder_4_out_0[11]),
    .out_12(decoder_4_out_0[12]), .out_13(decoder_4_out_0[13]), .out_14(decoder_4_out_0[14]),
    .out_15(decoder_4_out_0[15]), .out_16(decoder_4_out_0[16]), .out_17(decoder_4_out_0[17]),
    .out_18(decoder_4_out_0[18]), .out_19(decoder_4_out_0[19]), .out_20(decoder_4_out_0[20]),
    .out_21(decoder_4_out_0[21]), .out_22(decoder_4_out_0[22]), .out_23(decoder_4_out_0[23]),
    .out_24(decoder_4_out_0[24]), .out_25(decoder_4_out_0[25]), .out_26(decoder_4_out_0[26]),
    .out_27(decoder_4_out_0[27]), .out_28(decoder_4_out_0[28]), .out_29(decoder_4_out_0[29]),
    .out_30(decoder_4_out_0[30]), .out_31(decoder_4_out_0[31]));
  assign driver_22_out = OP_SPECIAL1 ? decoder_4_out_0 : 32'bz;  // Driver driver_22
  PullDown #(.Bits(32)) pulldown_6 (.out(driver_22_out));

  // Other names for the same wires on the sheet: SREG_IMM8[6:0] = SREG_IMM7;
  //   SREG_IMM14[7:0] = {SREG_IMM8[7], SREG_IMM7};
  //   SREG_IMM_16[15:0] = {SREG_IMM16_HI, SREG_IMM14, SREG_IMM8[7], SREG_IMM7};
  //   SREG_IMM_21[15:0] = {SREG_IMM16_HI, SREG_IMM14, SREG_IMM8[7], SREG_IMM7}; SREG_IMM14_HI[5:0] = SREG_IMM14;
  //   SREG_IMM16_HI[5:0] = SREG_IMM14; CNT_PC[15:0] = IROM_ADDR[15:0]; REGF_AB[7:0] = REGF_A; REGF_B[7:0] = REGF_AB;
  //   REGF_IJ[7:0] = REGF_I; REGF_J[7:0] = REGF_IJ; STACK_XY[7:0] = STACK_X; STACK_Y[7:0] = STACK_XY

  // Notes on the sheet:
  //   op-decode
  //   DATA bus
  //   Control registers
  //   ROM/RAM address
  //   Register files
  //   Stacks
  //   ALUs
  //   Program counter/jump/branch
endmodule
