// Digital circuit t3lc_mini.dig as structural Verilog
module t3lc_mini (
  input  [7:0] IROM_IN,
  input  CLK,
  input  ENA,
  input  [7:0] DATA_IN,
  output [7:0] IROM_ADDR,
  output [7:0] DATA_ADDR,
  output DROM_READ,
  output DRAM_READ,
  output DRAM_WRITE,
  output [7:0] DATA_OUT
);

  wire and_1_out, comparator_1_eq, decoder_1_out_2, decoder_1_out_3, decoder_1_out_4, decoder_1_out_5,
       decoder_1_out_6, decoder_1_out_7, decoder_1_out_9, decoder_1_out_10, decoder_1_out_11,
       decoder_1_out_12, decoder_1_out_13, decoder_1_out_14, decoder_1_out_15, not_1_out, or_1_out;
  wire [3:0] REG_IMM_LO_q;
  wire [7:0] alu_8_1_res, driver_1_out, driver_2_out, multiplexer_1_out, multiplexer_2_out, REG_A_q,
       REG_ALU_q, REG_B_q, REG_C_q;
  wire [7:4] REG_IMM_HI_q;

  not not_1 (not_1_out, IROM_IN[3]);
  assign driver_1_out = or_1_out ? DATA_IN : 8'bz;  // Driver driver_1
  Register #(.Bits(8)) REG_DATA (.D(driver_1_out), .C(CLK), .en(not_1_out), .Q(DATA_OUT));
  assign driver_1_out = ~or_1_out ? driver_2_out : 8'bz;  // DriverInvSel driverinvsel_1
  or or_1 (or_1_out, DRAM_READ, DROM_READ);
  Comparator #(.Bits(8)) comparator_1 (.a(DATA_OUT), .b({8{1'b0}}), .eq(comparator_1_eq));  // open: gt, lt
  Register #(.Bits(8)) REG_A (.D(DATA_OUT), .C(CLK), .en(decoder_1_out_15), .Q(REG_A_q));
  Register #(.Bits(8)) REG_B (.D(DATA_OUT), .C(CLK), .en(decoder_1_out_14), .Q(REG_B_q));
  Register #(.Bits(8)) REG_C (.D(DATA_OUT), .C(CLK), .en(decoder_1_out_13), .Q(REG_C_q));
  Register #(.Bits(4)) REG_IMM_LO (.D(IROM_IN[7:4]), .C(CLK), .en(decoder_1_out_12), .Q(REG_IMM_LO_q));
  Register #(.Bits(4)) REG_IMM_HI (.D(REG_IMM_LO_q), .C(CLK), .en(decoder_1_out_12), .Q(REG_IMM_HI_q));
  Register #(.Bits(8)) REG_ALU (.D(DATA_OUT), .C(CLK), .en(decoder_1_out_11), .Q(REG_ALU_q));
  Register #(.Bits(8)) REG_ADDR (.D(DATA_OUT), .C(CLK), .en(decoder_1_out_10), .Q(DATA_ADDR));
  and and_1 (and_1_out, decoder_1_out_9, comparator_1_eq);
  Decoder #(.Selector_Bits(4)) decoder_1 (
    .sel(IROM_IN[3:0]), .out_0(DRAM_READ), .out_1(DROM_READ), .out_2(decoder_1_out_2),
    .out_3(decoder_1_out_3), .out_4(decoder_1_out_4), .out_5(decoder_1_out_5), .out_6(decoder_1_out_6),
    .out_7(decoder_1_out_7), .out_8(DRAM_WRITE), .out_9(decoder_1_out_9), .out_10(decoder_1_out_10),
    .out_11(decoder_1_out_11), .out_12(decoder_1_out_12), .out_13(decoder_1_out_13),
    .out_14(decoder_1_out_14), .out_15(decoder_1_out_15));
  CounterPreset #(.Bits(8), .isProgramCounter("true")) CNT_PC (
    .en(ENA), .C(CLK), .dir(1'b0), .in(DATA_ADDR), .ld(and_1_out), .clr(1'b0), .out(IROM_ADDR));  // open: ovf
  Multiplexer #(.Selector_Bits(2), .Bits(8)) multiplexer_1 (
    .sel(REG_ALU_q[5:4]), .in_0(REG_A_q), .in_1(REG_B_q), .in_2(REG_C_q),
    .in_3({REG_IMM_HI_q, REG_IMM_LO_q}), .out(multiplexer_1_out));
  Multiplexer #(.Selector_Bits(2), .Bits(8)) multiplexer_2 (
    .sel(REG_ALU_q[7:6]), .in_0(REG_A_q), .in_1(REG_B_q), .in_2(REG_C_q),
    .in_3({REG_IMM_HI_q, REG_IMM_LO_q}), .out(multiplexer_2_out));
  alu_8 alu_8_1 (.A(multiplexer_1_out), .B(multiplexer_2_out), .OP(REG_ALU_q[3:0]), .RES(alu_8_1_res));  // open: C
  assign driver_2_out = decoder_1_out_7 ? REG_A_q : 8'bz;  // Driver driver_2
  assign driver_2_out = decoder_1_out_6 ? REG_B_q : 8'bz;  // Driver driver_3
  assign driver_2_out = decoder_1_out_5 ? REG_C_q : 8'bz;  // Driver driver_4
  assign driver_2_out = decoder_1_out_4 ? {REG_IMM_HI_q, REG_IMM_LO_q} : 8'bz;  // Driver driver_5
  assign driver_2_out = decoder_1_out_3 ? alu_8_1_res : 8'bz;  // Driver driver_6
  assign driver_2_out = decoder_1_out_2 ? IROM_ADDR : 8'bz;  // Driver driver_7
endmodule
