// Digital circuit testbed_huge.dig as structural Verilog
module testbed_huge (
  input  CLK
);

  wire and_1_out, and_2_out, and_3_out, and_4_out, and_5_out, and_6_out, and_7_out, decoder_1_out_0,
       decoder_1_out_1, decoder_1_out_2, decoder_1_out_3, register_1_q, t3lc_huge_1_ext_read,
       t3lc_huge_1_ext_write;
  wire [5:0] t3lc_huge_1_ext_sel;
  wire [7:0] DRAM_d, graphiccard_1_d, IROM_d, t3lc_huge_1_ext_out;
  wire [23:0] t3lc_huge_1_ext_addr, t3lc_huge_1_irom_addr;

  t3lc_huge t3lc_huge_1 (
    .CLK(CLK), .INTR(1'b0), .EXT_IN(DRAM_d), .IROM_IN(IROM_d), .IROM_ADDR(t3lc_huge_1_irom_addr),
    .EXT_READ(t3lc_huge_1_ext_read), .EXT_WRITE(t3lc_huge_1_ext_write), .EXT_OUT(t3lc_huge_1_ext_out),
    .EXT_SEL(t3lc_huge_1_ext_sel), .EXT_ADDR(t3lc_huge_1_ext_addr));  // open: HALTED
  ROM #(.AddrBits(24), .isProgramMemory("true"), .Bits(8)) IROM (.A(t3lc_huge_1_irom_addr), .sel(1'b1), .D(IROM_d));
  Decoder #(.Selector_Bits(2)) decoder_1 (
    .sel(t3lc_huge_1_ext_sel[1:0]), .out_0(decoder_1_out_0), .out_1(decoder_1_out_1),
    .out_2(decoder_1_out_2), .out_3(decoder_1_out_3));
  and and_1 (and_1_out, t3lc_huge_1_ext_write, decoder_1_out_0);
  and and_2 (and_2_out, t3lc_huge_1_ext_read, decoder_1_out_0);
  and and_3 (and_3_out, t3lc_huge_1_ext_write, decoder_1_out_1);
  and and_4 (and_4_out, t3lc_huge_1_ext_read, decoder_1_out_1);
  and and_5 (and_5_out, t3lc_huge_1_ext_write, decoder_1_out_2);
  and and_6 (and_6_out, t3lc_huge_1_ext_read, decoder_1_out_2);
  and and_7 (and_7_out, t3lc_huge_1_ext_write, decoder_1_out_3);
  Register register_1 (.D(t3lc_huge_1_ext_out[0]), .C(CLK), .en(and_7_out), .Q(register_1_q));
  RAMDualPort #(.AddrBits(24), .Bits(8)) DRAM (
    .A(t3lc_huge_1_ext_addr), .Din(t3lc_huge_1_ext_out), .str(and_1_out), .C(CLK), .ld(and_2_out), .D(DRAM_d));
  Telnet #(.telnetEscape("false"), .port(2323)) telnet_1 (
    .in(t3lc_huge_1_ext_out), .C(CLK), .wr(and_3_out), .rd(and_4_out), .out(DRAM_d));  // open: av
  GraphicCard #(.Bits(8)) graphiccard_1 (
    .A(t3lc_huge_1_ext_addr), .str(and_5_out), .C(CLK), .ld(and_6_out), .B(register_1_q), .D(graphiccard_1_d));
  assign DRAM_d[0] = and_6_out ? graphiccard_1_d[0] : 1'bz;  // Driver driver_1
  assign graphiccard_1_d[0] = and_5_out ? t3lc_huge_1_ext_out[0] : 1'bz;  // Driver driver_2
  // Pins of 1 and 8 bits meet at DRAM_d
  // Pins of 1 and 8 bits meet at t3lc_huge_1_ext_out
  // Pins of 1 and 8 bits meet at graphiccard_1_d

  // Notes on the sheet:
  //   CLK: Hz: 2147483647
endmodule
