// Digital circuit testbed_mini.dig as structural Verilog
module testbed_mini (
  input  clk
);

  wire and_1_out, and_2_out, comparator_1_eq, not_1_out, not_2_out, t3lc_mini_1_dram_read,
       t3lc_mini_1_dram_write, t3lc_mini_1_drom_read;
  wire [7:0] DRAM_d, driver_1_out, DROM_d, IROM_d, t3lc_mini_1_data_addr, t3lc_mini_1_data_out,
       t3lc_mini_1_irom_addr, telnet_1_out;

  ROM #(.AddrBits(8), .Bits(8), .isProgramMemory("true")) IROM (.A(t3lc_mini_1_irom_addr), .sel(1'b1), .D(IROM_d));
  t3lc_mini t3lc_mini_1 (
    .IROM_IN(IROM_d), .CLK(clk), .ENA(1'b1), .DATA_IN(driver_1_out), .IROM_ADDR(t3lc_mini_1_irom_addr),
    .DATA_ADDR(t3lc_mini_1_data_addr), .DROM_READ(t3lc_mini_1_drom_read), .DRAM_READ(t3lc_mini_1_dram_read),
    .DRAM_WRITE(t3lc_mini_1_dram_write), .DATA_OUT(t3lc_mini_1_data_out));
  Comparator #(.Bits(8)) comparator_1 (.a(t3lc_mini_1_data_addr), .b({8{1'b1}}), .eq(comparator_1_eq));  // open: gt, lt
  and and_1 (and_1_out, comparator_1_eq, t3lc_mini_1_dram_read);
  and and_2 (and_2_out, comparator_1_eq, t3lc_mini_1_dram_write);
  ROM #(.AddrBits(8), .Bits(8)) DROM (.A(t3lc_mini_1_data_addr), .sel(t3lc_mini_1_drom_read), .D(DROM_d));
  Telnet #(.telnetEscape("false"), .port(2323)) telnet_1 (
    .in(t3lc_mini_1_data_out), .C(clk), .wr(and_1_out), .rd(and_2_out), .out(telnet_1_out));  // open: av
  not not_1 (not_1_out, and_2_out);
  not not_2 (not_2_out, and_1_out);
  RAMDualPort #(.AddrBits(8), .Bits(8)) DRAM (
    .A(t3lc_mini_1_data_addr), .Din(t3lc_mini_1_data_out), .str(not_2_out), .C(clk), .ld(not_1_out),
    .D(DRAM_d));
  assign driver_1_out = and_2_out ? telnet_1_out : 8'bz;  // Driver driver_1
  assign driver_1_out = not_1_out ? DRAM_d : 8'bz;  // Driver driver_2
  assign driver_1_out = t3lc_mini_1_drom_read ? DROM_d : 8'bz;  // Driver driver_3

  // Notes on the sheet:
  //   clk: Hz: 2147483647
endmodule
