// Logisim project t3lc.circ as structural Verilog: 11 circuits, main circuit testbed_huge
module alu_8 (
  input  [3:0] OP,
  input  [7:0] A,
  input  [7:0] B,
  output [7:0] RES,
  output [7:0] CARRY
);

  wire adder_1_cout, comparator_1_eq, comparator_1_gt, decoder_1_out0, decoder_1_out1, decoder_1_out2,
       decoder_1_out3, decoder_1_out4, decoder_1_out5, decoder_1_out6, decoder_1_out7, decoder_1_out8,
       decoder_1_out9, decoder_1_out10, decoder_1_out11, decoder_1_out12, decoder_1_out13, decoder_1_out14,
       decoder_1_out15, subtractor_1_bout;
  wire [7:0] adder_1_out, and_1_out, bit_extender_1_out, bit_extender_2_out, bit_extender_3_out,
       bit_extender_4_out, divider_1_out, divider_1_rem, multiplier_1_cout, multiplier_1_out, negator_1_out,
       not_1_out, or_1_out, shifter_1_out, shifter_2_out, shifter_3_out, shifter_4_out, subtractor_1_out,
       xor_1_out;

  Adder adder_1 (.a(A), .b(B), .out(adder_1_out), .cout(adder_1_cout));  // open: cin
  Subtractor subtractor_1 (.a(A), .b(B), .out(subtractor_1_out), .bout(subtractor_1_bout));  // open: bin
  Multiplier multiplier_1 (.a(A), .b(B), .out(multiplier_1_out), .cout(multiplier_1_cout));  // open: cin
  Divider divider_1 (.a(A), .b(B), .out(divider_1_out), .rem(divider_1_rem));  // open: upper
  assign and_1_out = A & B;  // AND_Gate and_1, 8 bits wide
  assign or_1_out = A | B;  // OR_Gate or_1, 8 bits wide
  assign xor_1_out = A ^ B;  // XOR_Gate xor_1, 8 bits wide
  assign not_1_out = ~A;  // NOT_Gate not_1, 8 bits wide
  Shifter shifter_1 (.in(A), .\dist (3'b001), .out(shifter_1_out));
  Shifter shifter_2 (.in(A), .\dist (B[2:0]), .out(shifter_2_out));
  Shifter #(.shift("lr")) shifter_3 (.in(A), .\dist (3'b001), .out(shifter_3_out));
  Shifter #(.shift("lr")) shifter_4 (.in(A), .\dist (B[2:0]), .out(shifter_4_out));
  Negator negator_1 (.in(A), .out(negator_1_out));
  Comparator comparator_1 (.a(A), .b(B), .gt(comparator_1_gt), .eq(comparator_1_eq));  // open: lt
  assign bit_extender_1_out = {{7{1'b0}}, adder_1_cout};  // Bit_Extender bit_extender_1
  assign bit_extender_2_out = {{7{1'b0}}, subtractor_1_bout};  // Bit_Extender bit_extender_2
  assign bit_extender_3_out = {{7{1'b0}}, comparator_1_gt};  // Bit_Extender bit_extender_3
  assign bit_extender_4_out = {{7{1'b0}}, comparator_1_eq};  // Bit_Extender bit_extender_4
  assign CARRY = decoder_1_out0 ? bit_extender_1_out : 8'bz;  // Controlled_Buffer controlled_buffer_1
  assign CARRY = decoder_1_out1 ? bit_extender_2_out : 8'bz;  // Controlled_Buffer controlled_buffer_2
  assign CARRY = decoder_1_out2 ? multiplier_1_cout : 8'bz;  // Controlled_Buffer controlled_buffer_3
  assign CARRY = decoder_1_out3 ? divider_1_rem : 8'bz;  // Controlled_Buffer controlled_buffer_4
  Decoder #(.enable("false"), .select(4)) decoder_1 (
    .out0(decoder_1_out0), .out1(decoder_1_out1), .out2(decoder_1_out2), .out3(decoder_1_out3),
    .out4(decoder_1_out4), .out5(decoder_1_out5), .out6(decoder_1_out6), .out7(decoder_1_out7),
    .out8(decoder_1_out8), .out9(decoder_1_out9), .out10(decoder_1_out10), .out11(decoder_1_out11),
    .out12(decoder_1_out12), .out13(decoder_1_out13), .out14(decoder_1_out14), .out15(decoder_1_out15),
    .sel(OP));
  assign RES = decoder_1_out0 ? adder_1_out : 8'bz;  // Controlled_Buffer controlled_buffer_5
  assign RES = decoder_1_out1 ? subtractor_1_out : 8'bz;  // Controlled_Buffer controlled_buffer_6
  assign RES = decoder_1_out2 ? multiplier_1_out : 8'bz;  // Controlled_Buffer controlled_buffer_7
  assign RES = decoder_1_out3 ? divider_1_out : 8'bz;  // Controlled_Buffer controlled_buffer_8
  assign RES = decoder_1_out4 ? and_1_out : 8'bz;  // Controlled_Buffer controlled_buffer_9
  assign RES = decoder_1_out5 ? or_1_out : 8'bz;  // Controlled_Buffer controlled_buffer_10
  assign RES = decoder_1_out6 ? xor_1_out : 8'bz;  // Controlled_Buffer controlled_buffer_11
  assign RES = decoder_1_out7 ? not_1_out : 8'bz;  // Controlled_Buffer controlled_buffer_12
  assign RES = decoder_1_out8 ? shifter_1_out : 8'bz;  // Controlled_Buffer controlled_buffer_13
  assign RES = decoder_1_out9 ? shifter_2_out : 8'bz;  // Controlled_Buffer controlled_buffer_14
  assign RES = decoder_1_out10 ? shifter_3_out : 8'bz;  // Controlled_Buffer controlled_buffer_15
  assign RES = decoder_1_out11 ? shifter_4_out : 8'bz;  // Controlled_Buffer controlled_buffer_16
  assign RES = decoder_1_out12 ? negator_1_out : 8'bz;  // Controlled_Buffer controlled_buffer_17
  assign RES = decoder_1_out13 ? bit_extender_3_out : 8'bz;  // Controlled_Buffer controlled_buffer_18
  assign RES = decoder_1_out14 ? bit_extender_4_out : 8'bz;  // Controlled_Buffer controlled_buffer_19
  assign RES = decoder_1_out15 ? A : 8'bz;  // Controlled_Buffer controlled_buffer_20
endmodule

module alu_16 (
  input  [3:0] OP,
  input  [15:0] A,
  input  [15:0] B,
  output [15:0] RES
);

  wire comparator_1_eq, comparator_1_gt, decoder_1_out0, decoder_1_out1, decoder_1_out2, decoder_1_out3,
       decoder_1_out4, decoder_1_out5, decoder_1_out6, decoder_1_out7, decoder_1_out8, decoder_1_out9,
       decoder_1_out10, decoder_1_out11, decoder_1_out12, decoder_1_out13, decoder_1_out14, decoder_1_out15;
  wire [15:0] adder_1_out, and_1_out, bit_extender_1_out, bit_extender_2_out, divider_1_out,
       multiplier_1_out, negator_1_out, not_1_out, or_1_out, shifter_1_out, shifter_2_out, shifter_3_out,
       shifter_4_out, subtractor_1_out, xor_1_out;

  Adder #(.width(16)) adder_1 (.a(A), .b(B), .out(adder_1_out));  // open: cin, cout
  Subtractor #(.width(16)) subtractor_1 (.a(A), .b(B), .out(subtractor_1_out));  // open: bin, bout
  Multiplier #(.width(16)) multiplier_1 (.a(A), .b(B), .out(multiplier_1_out));  // open: cin, cout
  Divider #(.width(16)) divider_1 (.a(A), .b(B), .out(divider_1_out));  // open: upper, rem
  assign and_1_out = A & B;  // AND_Gate and_1, 16 bits wide
  assign or_1_out = A | B;  // OR_Gate or_1, 16 bits wide
  assign xor_1_out = A ^ B;  // XOR_Gate xor_1, 16 bits wide
  assign not_1_out = ~A;  // NOT_Gate not_1, 16 bits wide
  Shifter #(.width(16)) shifter_1 (.in(A), .\dist (4'b0001), .out(shifter_1_out));
  Shifter #(.width(16)) shifter_2 (.in(A), .\dist (B[3:0]), .out(shifter_2_out));
  Shifter #(.shift("lr"), .width(16)) shifter_3 (.in(A), .\dist (4'b0001), .out(shifter_3_out));
  Shifter #(.shift("lr"), .width(16)) shifter_4 (.in(A), .\dist (B[3:0]), .out(shifter_4_out));
  Negator #(.width(16)) negator_1 (.in(A), .out(negator_1_out));
  Comparator #(.width(16)) comparator_1 (.a(A), .b(B), .gt(comparator_1_gt), .eq(comparator_1_eq));  // open: lt
  assign bit_extender_1_out = {{15{1'b0}}, comparator_1_gt};  // Bit_Extender bit_extender_1
  assign bit_extender_2_out = {{15{1'b0}}, comparator_1_eq};  // Bit_Extender bit_extender_2
  Decoder #(.enable("false"), .select(4)) decoder_1 (
    .out0(decoder_1_out0), .out1(decoder_1_out1), .out2(decoder_1_out2), .out3(decoder_1_out3),
    .out4(decoder_1_out4), .out5(decoder_1_out5), .out6(decoder_1_out6), .out7(decoder_1_out7),
    .out8(decoder_1_out8), .out9(decoder_1_out9), .out10(decoder_1_out10), .out11(decoder_1_out11),
    .out12(decoder_1_out12), .out13(decoder_1_out13), .out14(decoder_1_out14), .out15(decoder_1_out15),
    .sel(OP));
  assign RES = decoder_1_out0 ? adder_1_out : 16'bz;  // Controlled_Buffer controlled_buffer_1
  assign RES = decoder_1_out1 ? subtractor_1_out : 16'bz;  // Controlled_Buffer controlled_buffer_2
  assign RES = decoder_1_out2 ? multiplier_1_out : 16'bz;  // Controlled_Buffer controlled_buffer_3
  assign RES = decoder_1_out3 ? divider_1_out : 16'bz;  // Controlled_Buffer controlled_buffer_4
  assign RES = decoder_1_out4 ? and_1_out : 16'bz;  // Controlled_Buffer controlled_buffer_5
  assign RES = decoder_1_out5 ? or_1_out : 16'bz;  // Controlled_Buffer controlled_buffer_6
  assign RES = decoder_1_out6 ? xor_1_out : 16'bz;  // Controlled_Buffer controlled_buffer_7
  assign RES = decoder_1_out7 ? not_1_out : 16'bz;  // Controlled_Buffer controlled_buffer_8
  assign RES = decoder_1_out8 ? shifter_1_out : 16'bz;  // Controlled_Buffer controlled_buffer_9
  assign RES = decoder_1_out9 ? shifter_2_out : 16'bz;  // Controlled_Buffer controlled_buffer_10
  assign RES = decoder_1_out10 ? shifter_3_out : 16'bz;  // Controlled_Buffer controlled_buffer_11
  assign RES = decoder_1_out11 ? shifter_4_out : 16'bz;  // Controlled_Buffer controlled_buffer_12
  assign RES = decoder_1_out12 ? negator_1_out : 16'bz;  // Controlled_Buffer controlled_buffer_13
  assign RES = decoder_1_out13 ? bit_extender_1_out : 16'bz;  // Controlled_Buffer controlled_buffer_14
  assign RES = decoder_1_out14 ? bit_extender_2_out : 16'bz;  // Controlled_Buffer controlled_buffer_15
  assign RES = decoder_1_out15 ? A : 16'bz;  // Controlled_Buffer controlled_buffer_16
endmodule

module stack (
  input  WRITE_TOS,
  input  READ_TOS,
  input  RESET,
  input  [7:0] DATA_IN,
  input  CLK,
  input  PUSH,
  input  POP,
  input  LOAD_SP,
  input  [7:0] SP_IN,
  output [7:0] DATA_OUT,
  output [7:0] SP_OUT
);

  wire or_1_out, or_2_out, or_3_out, por_1_out;

  POR por_1 (.out(por_1_out));
  or or_1 (or_1_out, por_1_out, RESET);
  or or_2 (or_2_out, PUSH, POP);
  Counter STACK_POINTER (
    .clr(or_1_out), .load(LOAD_SP), .up(PUSH), .count(or_2_out), .clk(CLK), .D(SP_IN), .Q(SP_OUT));  // open: carry
  or or_3 (or_3_out, READ_TOS, or_1_out);
  RAM #(.asyncread("true"), .clearpin("true")) STACK_MEM (
    .addr(SP_OUT), .we(WRITE_TOS), .oe(or_3_out), .clk(CLK), .din(DATA_IN), .dout(DATA_OUT), .clr(or_1_out));
endmodule

module register_file (
  input  [7:0] ADDR_IN,
  input  [7:0] DATA_IN,
  input  CLK,
  input  WRITE_ADDR,
  input  WRITE_MEM,
  input  READ_MEM,
  input  RESET,
  output [7:0] DATA_OUT
);

  wire or_1_out, or_2_out, por_1_out;
  wire [7:0] REGF_INDEX_q;

  POR por_1 (.out(por_1_out));
  Register REGF_INDEX (.D(ADDR_IN), .en(WRITE_ADDR), .clk(CLK), .Q(REGF_INDEX_q), .clr(or_2_out));
  or or_1 (or_1_out, READ_MEM, por_1_out);
  or or_2 (or_2_out, por_1_out, RESET);
  RAM #(.asyncread("true"), .clearpin("true")) REGF_MEMORY (
    .addr(REGF_INDEX_q), .we(WRITE_MEM), .oe(or_1_out), .clk(CLK), .din(DATA_IN), .dout(DATA_OUT),
    .clr(or_2_out));
endmodule

module t3lc_mini (
  input  [7:0] ROM_VALUE,
  input  [7:0] DATA_IN,
  input  CLK,
  input  RESET,
  output RAM_WRITE,
  output RAM_READ,
  output [7:0] DATA_OUT,
  output HALT,
  output [7:0] RAM_ADDR,
  output [7:0] ROM_ADDR
);

  wire and_1_out, comparator_1_eq, decoder_1_out0, decoder_1_out1, decoder_1_out2, decoder_1_out3,
       decoder_1_out4, decoder_1_out5, decoder_1_out6, decoder_2_out0, decoder_2_out1, decoder_2_out2,
       decoder_2_out4, decoder_2_out5, decoder_2_out6, not_1_out, or_1_out, SREG_IMM_p3;
  wire [3:0] SREG_IMM_p6, SREG_IMM_p7, SREG_IMM_p8, SREG_IMM_p9;
  wire [7:0] alu_8_1_res, controlled_buffer_1_out, multiplexer_1_out, multiplexer_2_out, REG_A_q, REG_ALU_q,
       REG_B_q, REG_C_q;

  assign controlled_buffer_1_out = RAM_READ ? DATA_IN : 8'bz;  // Controlled_Buffer controlled_buffer_1
  not not_1 (not_1_out, ROM_VALUE[3]);
  Decoder #(.select(3)) decoder_1 (
    .out0(decoder_1_out0), .out1(decoder_1_out1), .out2(decoder_1_out2), .out3(decoder_1_out3),
    .out4(decoder_1_out4), .out5(decoder_1_out5), .out6(decoder_1_out6), .out7(RAM_WRITE),
    .sel(ROM_VALUE[2:0]), .en(ROM_VALUE[3]));
  Register REG_A (.D({SREG_IMM_p7, SREG_IMM_p6}), .en(decoder_1_out0), .clk(CLK), .Q(REG_A_q), .clr(RESET));
  Register REG_B (.D({SREG_IMM_p7, SREG_IMM_p6}), .en(decoder_1_out1), .clk(CLK), .Q(REG_B_q), .clr(RESET));
  Register REG_C (.D({SREG_IMM_p7, SREG_IMM_p6}), .en(decoder_1_out2), .clk(CLK), .Q(REG_C_q), .clr(RESET));
  // Shift_Register #(.length(2), .width(4)) SREG_IMM: pin names not known; wires that end beside it: RESET, decoder_1_out3, SREG_IMM_p3, CLK, ROM_VALUE[7:4], SREG_IMM_p6, SREG_IMM_p7, SREG_IMM_p8, SREG_IMM_p9
  Register REG_ALU (.D({SREG_IMM_p7, SREG_IMM_p6}), .en(decoder_1_out4), .clk(CLK), .Q(REG_ALU_q), .clr(RESET));
  Register REG_ADDR (.D({SREG_IMM_p7, SREG_IMM_p6}), .en(decoder_1_out5), .clk(CLK), .Q(RAM_ADDR), .clr(RESET));
  Comparator comparator_1 (.a({8{1'b0}}), .b({SREG_IMM_p7, SREG_IMM_p6}), .eq(comparator_1_eq));  // open: gt, lt
  Counter CNT_PC (.clr(RESET), .load(or_1_out), .clk(CLK), .D(RAM_ADDR), .Q(ROM_ADDR));  // open: up, count, carry
  Register REG_DATA (
    .D(controlled_buffer_1_out), .en(not_1_out), .clk(CLK), .Q({SREG_IMM_p7, SREG_IMM_p6}), .clr(RESET));
  and and_1 (and_1_out, decoder_2_out5, comparator_1_eq);
  or or_1 (or_1_out, and_1_out, decoder_1_out6);
  Multiplexer #(.select(2), .width(8)) multiplexer_1 (
    .in0(REG_A_q), .in1(REG_B_q), .in2(REG_C_q), .in3({SREG_IMM_p9, SREG_IMM_p8}), .out(multiplexer_1_out),
    .sel(REG_ALU_q[7:6]));
  Multiplexer #(.select(2), .width(8)) multiplexer_2 (
    .in0(REG_A_q), .in1(REG_B_q), .in2(REG_C_q), .in3({SREG_IMM_p9, SREG_IMM_p8}), .out(multiplexer_2_out),
    .sel(REG_ALU_q[5:4]));
  Decoder #(.select(3)) decoder_2 (
    .out0(decoder_2_out0), .out1(decoder_2_out1), .out2(decoder_2_out2), .out3(SREG_IMM_p3),
    .out4(decoder_2_out4), .out5(decoder_2_out5), .out6(decoder_2_out6), .out7(RAM_READ),
    .sel(ROM_VALUE[2:0]), .en(not_1_out));
  assign controlled_buffer_1_out = decoder_2_out0 ? REG_A_q : 8'bz;  // Controlled_Buffer controlled_buffer_2
  assign controlled_buffer_1_out = decoder_2_out1 ? REG_B_q : 8'bz;  // Controlled_Buffer controlled_buffer_3
  assign controlled_buffer_1_out = decoder_2_out2 ? REG_C_q : 8'bz;  // Controlled_Buffer controlled_buffer_4
  assign controlled_buffer_1_out = SREG_IMM_p3 ? {SREG_IMM_p9, SREG_IMM_p8} : 8'bz;  // Controlled_Buffer controlled_buffer_5
  assign controlled_buffer_1_out = decoder_2_out6 ? ROM_ADDR : 8'bz;  // Controlled_Buffer controlled_buffer_6
  assign DATA_OUT = RAM_WRITE ? controlled_buffer_1_out : 8'bz;  // Controlled_Buffer controlled_buffer_7
  and and_2 (HALT, decoder_1_out4, comparator_1_eq);
  assign controlled_buffer_1_out = decoder_2_out4 ? alu_8_1_res : 8'bz;  // Controlled_Buffer controlled_buffer_8
  alu_8 alu_8_1 (.OP(REG_ALU_q[3:0]), .A(multiplexer_1_out), .B(multiplexer_2_out), .RES(alu_8_1_res));  // open: CARRY
endmodule

module t3lc_medium (
  input  CLK,
  input  RESET,
  input  [7:0] ROM_VALUE,
  input  [7:0] DATA_IN,
  output RAM_WRITE,
  output RAM_READ,
  output [7:0] DATA_OUT,
  output HALTED,
  output [15:0] ROM_ADDR,
  output [15:0] RAM_ADDR
);

  wire ALU_AB_READ, ALU_IJ_READ, ALU_READ, and_3_out, and_13_out, BRANCH, comparator_1_eq, decoder_2_out9,
       HALT, HALT_qn, IMM_PUSH, JUMP, LAST_IMM_q, not_1_out, OP_IMM_READ, or_1_out, or_2_out, or_6_out, POP,
       PUSH, REG_IMM_READ, REGF_A_ADDR_WRITE, REGF_A_MEM_WRITE, REGF_A_READ, REGF_B_ADDR_WRITE,
       REGF_B_MEM_WRITE, REGF_B_READ, REGF_I_ADDR_WRITE, REGF_I_MEM_WRITE, REGF_I_READ, REGF_J_ADDR_WRITE,
       REGF_J_MEM_WRITE, REGF_J_READ, RESET_ALU, SPECIAL_OP, STACK_TOS_READ, STACK_TOS_WRITE;
  wire [6:0] REG_IMM;
  wire [7:0] alu_8_1_res, bit_extender_1_out, bit_extender_2_out, bit_extender_3_out, bit_extender_4_out,
       bit_extender_6_out, controlled_buffer_1_out, controlled_buffer_3_out, decoder_1_out0,
       multiplexer_1_out, multiplexer_2_out, multiplexer_3_out, OP_IMM, REGF_A, TOS;
  wire [8:0] bit_extender_5_out, decoder_2_out0;
  wire [15:8] REGF_AB;

  not not_1 (not_1_out, ROM_VALUE[7]);
  assign controlled_buffer_1_out = RAM_READ ? DATA_IN : 8'bz;  // Controlled_Buffer controlled_buffer_1
  Decoder #(.select(3)) decoder_1 (
    .out0(decoder_1_out0[0]), .out1(decoder_1_out0[1]), .out2(decoder_1_out0[2]), .out3(decoder_1_out0[3]),
    .out4(decoder_1_out0[4]), .out5(decoder_1_out0[5]), .out6(decoder_1_out0[6]), .out7(decoder_1_out0[7]),
    .sel(ROM_VALUE[6:4]), .en(not_1_out));
  assign {RAM_WRITE, REGF_B_ADDR_WRITE, REGF_A_ADDR_WRITE, STACK_TOS_WRITE, REGF_J_MEM_WRITE, REGF_I_MEM_WRITE, REGF_B_MEM_WRITE, REGF_A_MEM_WRITE} = decoder_1_out0 & ~bit_extender_1_out;  // AND_Gate and_1, 8 bits wide
  assign bit_extender_1_out = {{7{SPECIAL_OP}}, SPECIAL_OP};  // Bit_Extender bit_extender_1
  Register #(.width(7)) u_REG_IMM (.D(ROM_VALUE[6:0]), .en(ROM_VALUE[7]), .clk(CLK), .Q(REG_IMM), .clr(RESET));
  assign bit_extender_2_out = {{1{1'b0}}, REG_IMM};  // Bit_Extender bit_extender_2
  assign bit_extender_3_out = {{1{1'b0}}, REG_IMM};  // Bit_Extender bit_extender_3
  Multiplexer #(.select(3), .width(8)) multiplexer_1 (
    .in0(REGF_A), .in1(REGF_AB), .in2(RAM_ADDR[7:0]), .in3(RAM_ADDR[15:8]), .in4(ROM_ADDR[7:0]),
    .in5(ROM_ADDR[15:8]), .in6(TOS), .in7(REGF_A), .out(multiplexer_1_out), .sel(REG_IMM[6:4]));
  Multiplexer #(.width(8)) multiplexer_2 (
    .in0(controlled_buffer_1_out), .in1(bit_extender_4_out), .out(multiplexer_2_out), .sel(IMM_PUSH));
  assign bit_extender_4_out = {{1{1'b0}}, REG_IMM};  // Bit_Extender bit_extender_4
  D_Flip_Flop LAST_IMM (.D(ROM_VALUE[7]), .clk(CLK), .Q(LAST_IMM_q), .reset(RESET));  // open: Qn, preset
  Multiplexer #(.select(3), .width(8)) multiplexer_3 (
    .in0(REGF_AB), .in1(REGF_A), .in2(RAM_ADDR[15:8]), .in3(RAM_ADDR[7:0]), .in4(ROM_ADDR[7:0]),
    .in5(ROM_ADDR[15:8]), .in6(REGF_A), .in7(TOS), .out(multiplexer_3_out), .sel(REG_IMM[6:4]));
  or or_1 (or_1_out, PUSH, IMM_PUSH);
  or or_2 (or_2_out, IMM_PUSH, STACK_TOS_WRITE);
  and and_2 (IMM_PUSH, ROM_VALUE[7], LAST_IMM_q);
  and and_3 (and_3_out, ~RAM_WRITE, ~SPECIAL_OP, ~RAM_READ);  // AND_Gate
  assign controlled_buffer_1_out = and_3_out ? controlled_buffer_3_out : 8'bz;  // Controlled_Buffer controlled_buffer_2
  register_file u_REGF_A (
    .ADDR_IN(controlled_buffer_1_out), .DATA_IN(controlled_buffer_1_out), .CLK(CLK), .WRITE_ADDR(RESET),
    .WRITE_MEM(REGF_A_ADDR_WRITE), .READ_MEM(REGF_A_MEM_WRITE), .RESET(REGF_A_READ), .DATA_OUT(REGF_A));
  register_file REGF_B (
    .ADDR_IN(controlled_buffer_1_out), .DATA_IN(controlled_buffer_1_out), .CLK(CLK), .WRITE_ADDR(RESET),
    .WRITE_MEM(REGF_B_ADDR_WRITE), .READ_MEM(REGF_B_MEM_WRITE), .RESET(REGF_B_READ), .DATA_OUT(REGF_AB));
  register_file REGF_I (
    .ADDR_IN(bit_extender_2_out), .DATA_IN(controlled_buffer_1_out), .CLK(CLK), .WRITE_ADDR(RESET),
    .WRITE_MEM(REGF_I_ADDR_WRITE), .READ_MEM(REGF_I_MEM_WRITE), .RESET(REGF_I_READ), .DATA_OUT(RAM_ADDR[7:0]));
  register_file REGF_J (
    .ADDR_IN(bit_extender_3_out), .DATA_IN(controlled_buffer_1_out), .CLK(CLK), .WRITE_ADDR(RESET),
    .WRITE_MEM(REGF_J_ADDR_WRITE), .READ_MEM(REGF_J_MEM_WRITE), .RESET(REGF_J_READ), .DATA_OUT(RAM_ADDR[15:8]));
  Decoder #(.select(4)) decoder_2 (
    .out0(decoder_2_out0[0]), .out1(decoder_2_out0[1]), .out2(decoder_2_out0[2]), .out3(decoder_2_out0[3]),
    .out4(decoder_2_out0[4]), .out5(decoder_2_out0[5]), .out6(decoder_2_out0[6]), .out7(decoder_2_out0[7]),
    .out8(decoder_2_out0[8]), .out9(decoder_2_out9), .out10(OP_IMM[7]), .out11(OP_IMM[6]), .out12(OP_IMM[5]),
    .out13(OP_IMM[4]), .out14(OP_IMM[3]), .out15(OP_IMM[0]), .sel(ROM_VALUE[3:0]), .en(not_1_out));
  assign bit_extender_5_out = {{8{SPECIAL_OP}}, SPECIAL_OP};  // Bit_Extender bit_extender_5
  assign bit_extender_6_out = {{1{1'b0}}, REG_IMM};  // Bit_Extender bit_extender_6
  assign controlled_buffer_3_out = REGF_A_READ ? REGF_A : 8'bz;  // Controlled_Buffer controlled_buffer_3
  assign controlled_buffer_3_out = REGF_B_READ ? REGF_AB : 8'bz;  // Controlled_Buffer controlled_buffer_4
  alu_8 alu_8_1 (.OP(REG_IMM[3:0]), .A(multiplexer_1_out), .B(multiplexer_3_out), .RES(alu_8_1_res));  // open: CARRY
  stack STACK_MEM (
    .WRITE_TOS(or_2_out), .READ_TOS(STACK_TOS_READ), .RESET(RESET), .DATA_IN(multiplexer_2_out), .CLK(CLK),
    .PUSH(or_1_out), .POP(POP), .DATA_OUT(TOS));  // open: LOAD_SP, SP_IN, SP_OUT
  and and_4 (HALT, decoder_2_out0[0], decoder_1_out0[0]);
  and and_5 (PUSH, decoder_2_out0[1], decoder_1_out0[1]);
  and and_6 (POP, decoder_2_out0[2], decoder_1_out0[2]);
  and and_7 (RESET_ALU, decoder_2_out0[3], decoder_1_out0[3]);
  and and_8 (BRANCH, decoder_2_out0[4], decoder_1_out0[4]);
  and and_9 (JUMP, decoder_2_out0[5], decoder_1_out0[5]);
  and and_10 (REGF_I_ADDR_WRITE, decoder_2_out0[6], decoder_1_out0[6]);
  and and_11 (REGF_J_ADDR_WRITE, decoder_2_out0[7], decoder_1_out0[7]);
  assign {REG_IMM_READ, RAM_READ, ALU_IJ_READ, ALU_AB_READ, STACK_TOS_READ, REGF_J_READ, REGF_I_READ, REGF_B_READ, REGF_A_READ} = decoder_2_out0 & ~bit_extender_5_out;  // AND_Gate and_12, 9 bits wide
  or or_3 (OP_IMM_READ, decoder_2_out9, OP_IMM[7], OP_IMM[6], OP_IMM[5], OP_IMM[4], OP_IMM[3], OP_IMM[0]);
  or or_4 (SPECIAL_OP, HALT, PUSH, POP, RESET_ALU, BRANCH, JUMP, REGF_I_ADDR_WRITE, REGF_J_ADDR_WRITE);
  assign controlled_buffer_3_out = OP_IMM_READ ? {OP_IMM[7:3], 2'b00, OP_IMM[0]} : 8'bz;  // Controlled_Buffer controlled_buffer_5
  assign controlled_buffer_3_out = REG_IMM_READ ? bit_extender_6_out : 8'bz;  // Controlled_Buffer controlled_buffer_6
  assign controlled_buffer_3_out = REGF_I_READ ? RAM_ADDR[7:0] : 8'bz;  // Controlled_Buffer controlled_buffer_7
  assign controlled_buffer_3_out = REGF_J_READ ? RAM_ADDR[15:8] : 8'bz;  // Controlled_Buffer controlled_buffer_8
  assign controlled_buffer_3_out = ALU_READ ? alu_8_1_res : 8'bz;  // Controlled_Buffer controlled_buffer_9
  assign controlled_buffer_3_out = STACK_TOS_READ ? TOS : 8'bz;  // Controlled_Buffer controlled_buffer_10
  or or_5 (ALU_READ, ALU_AB_READ, ALU_IJ_READ);
  assign DATA_OUT = RAM_WRITE ? controlled_buffer_3_out : 8'bz;  // Controlled_Buffer controlled_buffer_11
  Comparator comparator_1 (.a(TOS), .b({8{1'b0}}), .eq(comparator_1_eq));  // open: gt, lt
  D_Flip_Flop u_HALT (.D(HALT), .clk(CLK), .Q(HALTED), .Qn(HALT_qn), .reset(RESET));  // open: preset
  or or_6 (or_6_out, JUMP, and_13_out);
  and and_13 (and_13_out, BRANCH, comparator_1_eq);
  Counter #(.max('hffff), .width(16)) CNT_PC (
    .load(or_6_out), .D(RAM_ADDR), .count(HALT_qn), .Q(ROM_ADDR), .clk(CLK), .clr(RESET));  // open: carry, up

  // Other names for the same wires on the sheet: CNT_PC[15:0] = ROM_ADDR; REGF_AB[7:0] = REGF_A;
  //   REGF_B[7:0] = REGF_AB; REGF_I[7:0] = RAM_ADDR[7:0]; REGF_IJ[15:0] = RAM_ADDR; REGF_J[7:0] = RAM_ADDR[15:8]

  // Notes on the sheet:
  //   DATA BUS TARGET
  //   DATA BUS SOURCE
endmodule

module t3lc_huge (
  input  INTR,
  input  CLK,
  input  RESET,
  input  [7:0] IROM_VALUE,
  input  [7:0] DATA_IN,
  output DROM_READ,
  output PERI0_READ,
  output PERI0_WRITE,
  output PERI1_READ,
  output PERI1_WRITE,
  output PERI2_READ,
  output PERI2_WRITE,
  output DRAM_READ,
  output DRAM_WRITE,
  output [7:0] DATA_OUT,
  output HALTED,
  output [23:0] ADDR,
  output [23:0] ROM_ADDR
);

  wire ALU8_CARRY_READ, ALU8_RES_READ, ALU16_LATCH, ALU16_RES_HI_READ, ALU16_RES_LO_READ, and_4_out,
       and_5_out, and_6_out, and_7_out, BRANCH_A_EQZ, BRANCH_A_NEZ, BRANCH_B_EQZ, BRANCH_B_NEZ, BUS_EXT,
       comparator_1_eq, comparator_2_eq, HALT, HALT_qn, JUMP, JUMP_CTRL_WRITE, OP_IMM_READ, or_1_out,
       or_3_out, or_5_out, RAM_PAGE_READ, RAM_PAGE_WRITE, READ_DATA, REGF_A_ADDR_WRITE, REGF_A_MEM_WRITE,
       REGF_A_READ, REGF_B_ADDR_WRITE, REGF_B_MEM_WRITE, REGF_B_READ, REGF_I_ADDR_WRITE, REGF_I_MEM_WRITE,
       REGF_I_READ, REGF_J_ADDR_WRITE, REGF_J_MEM_WRITE, REGF_J_READ, ROM_PAGE_READ, ROM_PAGE_WRITE,
       SPECIAL_0, SPECIAL_OP1, SREG_IMM7_READ, SREG_IMM8_HI6_READ, SREG_IMM8_HI_READ, SREG_IMM8_LO_READ,
       STACK_X_POP, STACK_X_PUSH, STACK_X_SP_READ, STACK_X_SP_WRITE, STACK_X_TOS_READ, STACK_X_TOS_WRITE,
       STACK_Y_POP, STACK_Y_PUSH, STACK_Y_SP_READ, STACK_Y_SP_WRITE, STACK_Y_TOS_READ, STACK_Y_TOS_WRITE,
       WRITE_DATA;
  wire [1:0] multiplexer_5_out;
  wire [6:0] SREG_IMM7;
  wire [7:0] ALU_8BIT_carry, ALU_8BIT_res, bit_extender_2_out, bit_extender_3_out, controlled_buffer_1_out,
       multiplexer_1_out, multiplexer_2_out, OP_IMM, OP_IMM_VAL, REG_ADDR_PAGE_q, REG_DATA_q,
       REG_JUMP_CTRL_q, REGF_A, REGF_I, SREG_IMM8_HI, STACK_X_sp_out, STACK_X_TOS, STACK_Y_sp_out;
  wire [7:7] SREG_IMM8_LO;
  wire [15:0] ALU_16BIT_res, bit_extender_1_out, LOAD_PC_ADDR, multiplexer_3_out, multiplexer_4_out,
       register_1_q;
  wire [15:8] REGF_AB, REGF_IJ, STACK_XY_TOS;
  wire [17:0] SREG_IMM_21;
  wire [20:16] SREG_IMM21;
  wire [23:23] decoder_2_out23;
  wire [31:0] decoder_4_out0;
  wire [31:3] decoder_3_out3;
  wire [31:19] decoder_1_out19;

  and and_1 (WRITE_DATA, IROM_VALUE[5], ~IROM_VALUE[6], ~IROM_VALUE[7]);  // AND_Gate
  // Shift_Register #(.length(3), .width(7)) SREG_IMM: pin names not known; wires that end beside it: RESET, IROM_VALUE[7], CLK, IROM_VALUE[6:0], SREG_IMM7, {SREG_IMM8_HI[5:0], SREG_IMM8_LO[7]}, {SREG_IMM21, SREG_IMM8_HI[7:6]}
  Decoder #(.select(5)) decoder_1 (
    .out0(REGF_A_MEM_WRITE), .out1(REGF_B_MEM_WRITE), .out2(REGF_I_MEM_WRITE), .out3(REGF_J_MEM_WRITE),
    .out4(REGF_A_ADDR_WRITE), .out5(REGF_B_ADDR_WRITE), .out6(REGF_I_ADDR_WRITE), .out7(REGF_J_ADDR_WRITE),
    .out8(STACK_X_TOS_WRITE), .out9(STACK_X_SP_WRITE), .out10(STACK_Y_TOS_WRITE), .out11(STACK_Y_SP_WRITE),
    .out12(RAM_PAGE_WRITE), .out13(ROM_PAGE_WRITE), .out14(DRAM_WRITE), .out15(PERI0_WRITE),
    .out16(PERI1_WRITE), .out17(PERI2_WRITE), .out18(JUMP_CTRL_WRITE), .out19(decoder_1_out19[19]),
    .out20(decoder_1_out19[20]), .out21(decoder_1_out19[21]), .out22(decoder_1_out19[22]),
    .out23(decoder_1_out19[23]), .out24(decoder_1_out19[24]), .out25(decoder_1_out19[25]),
    .out26(decoder_1_out19[26]), .out27(decoder_1_out19[27]), .out28(decoder_1_out19[28]),
    .out29(decoder_1_out19[29]), .out30(decoder_1_out19[30]), .out31(decoder_1_out19[31]),
    .sel(IROM_VALUE[4:0]), .en(WRITE_DATA));
  or or_1 (or_1_out, DROM_READ, PERI0_READ, PERI1_READ, PERI2_READ, DRAM_READ);
  assign controlled_buffer_1_out = or_1_out ? DATA_IN : 8'bz;  // Controlled_Buffer controlled_buffer_1
  Register REG_DATA (.D(controlled_buffer_1_out), .en(READ_DATA), .clk(CLK), .Q(REG_DATA_q), .clr(RESET));
  Register REG_JUMP_CTRL (.D(REG_DATA_q), .en(JUMP_CTRL_WRITE), .clk(CLK), .Q(REG_JUMP_CTRL_q), .clr(RESET));
  Register REG_ADDR_PAGE (.D(REG_DATA_q), .en(RAM_PAGE_WRITE), .clk(CLK), .Q(REG_ADDR_PAGE_q), .clr(RESET));
  Register REG_ROM_PAGE (.D(REG_DATA_q), .en(ROM_PAGE_WRITE), .clk(CLK), .Q(ROM_ADDR[23:16]), .clr(RESET));
  Multiplexer #(.select(3), .width(8)) multiplexer_1 (
    .in0(REGF_A), .in1(REGF_AB), .in2(REGF_I), .in3(REGF_IJ), .in4(STACK_X_TOS), .in5(STACK_XY_TOS),
    .in6(SREG_IMM_21[17:10]), .in7(8'h1), .out(multiplexer_1_out), .sel(SREG_IMM_21[6:4]));
  Multiplexer #(.select(3), .width(8)) multiplexer_2 (
    .in0(REGF_A), .in1(REGF_AB), .in2(REGF_I), .in3(REGF_IJ), .in4(STACK_X_TOS), .in5(STACK_XY_TOS),
    .in6(SREG_IMM_21[17:10]), .in7(8'h1), .out(multiplexer_2_out), .sel(SREG_IMM_21[9:7]));
  Multiplexer #(.select(2), .width(16)) multiplexer_3 (
    .in0({REGF_AB, REGF_A}), .in1({REGF_IJ, REGF_I}), .in2({STACK_XY_TOS, STACK_X_TOS}),
    .in3(ROM_ADDR[15:0]), .out(multiplexer_3_out), .sel(SREG_IMM_21[5:4]));
  Multiplexer #(.select(2), .width(16)) multiplexer_4 (
    .in0({REGF_AB, REGF_A}), .in1({REGF_IJ, REGF_I}), .in2({STACK_XY_TOS, STACK_X_TOS}),
    .in3(ROM_ADDR[15:0]), .out(multiplexer_4_out), .sel(SREG_IMM_21[8:7]));
  Multiplexer #(.width(2)) multiplexer_5 (.in0(REG_JUMP_CTRL_q[1:0]), .in1(2'b00), .out(multiplexer_5_out), .sel(INTR));
  assign bit_extender_1_out = {{10{1'b0}}, REG_JUMP_CTRL_q[7:2]};  // Bit_Extender bit_extender_1
  and and_2 (READ_DATA, ~IROM_VALUE[5], IROM_VALUE[6], ~IROM_VALUE[7]);  // AND_Gate
  Multiplexer #(.select(2), .width(16)) multiplexer_6 (
    .in0(bit_extender_1_out), .in1({REGF_AB, REGF_A}), .in2({REGF_IJ, REGF_I}),
    .in3({STACK_XY_TOS, STACK_X_TOS}), .out(LOAD_PC_ADDR), .sel(multiplexer_5_out));
  assign ADDR = BUS_EXT ? {REG_ADDR_PAGE_q, REGF_IJ, REGF_I} : 24'bz;  // Controlled_Buffer controlled_buffer_2
  register_file u_REGF_A (
    .ADDR_IN(REG_DATA_q), .DATA_IN(REG_DATA_q), .CLK(CLK), .WRITE_ADDR(REGF_A_ADDR_WRITE),
    .WRITE_MEM(REGF_A_MEM_WRITE), .READ_MEM(REGF_A_READ), .RESET(RESET), .DATA_OUT(REGF_A));
  register_file REGF_B (
    .ADDR_IN(REG_DATA_q), .DATA_IN(REG_DATA_q), .CLK(CLK), .WRITE_ADDR(REGF_B_ADDR_WRITE),
    .WRITE_MEM(REGF_B_MEM_WRITE), .READ_MEM(REGF_B_READ), .RESET(RESET), .DATA_OUT(REGF_AB));
  register_file u_REGF_I (
    .ADDR_IN(REG_DATA_q), .DATA_IN(REG_DATA_q), .CLK(CLK), .WRITE_ADDR(REGF_I_ADDR_WRITE),
    .WRITE_MEM(REGF_I_MEM_WRITE), .READ_MEM(REGF_I_READ), .RESET(RESET), .DATA_OUT(REGF_I));
  register_file REGF_J (
    .ADDR_IN(REG_DATA_q), .DATA_IN(REG_DATA_q), .CLK(CLK), .WRITE_ADDR(REGF_J_ADDR_WRITE),
    .WRITE_MEM(REGF_J_MEM_WRITE), .READ_MEM(REGF_J_READ), .RESET(RESET), .DATA_OUT(REGF_IJ));
  Decoder #(.select(5)) decoder_2 (
    .out0(REGF_A_READ), .out1(REGF_B_READ), .out2(REGF_I_READ), .out3(REGF_J_READ), .out4(ALU8_RES_READ),
    .out5(ALU8_CARRY_READ), .out6(ALU16_RES_LO_READ), .out7(ALU16_RES_HI_READ), .out8(STACK_X_TOS_READ),
    .out9(STACK_X_SP_READ), .out10(STACK_Y_TOS_READ), .out11(STACK_Y_SP_READ), .out12(RAM_PAGE_READ),
    .out13(ROM_PAGE_READ), .out14(DRAM_READ), .out15(PERI0_READ), .out16(PERI1_READ), .out17(PERI2_READ),
    .out18(DROM_READ), .out19(SREG_IMM7_READ), .out20(SREG_IMM8_LO_READ), .out21(SREG_IMM8_HI6_READ),
    .out22(SREG_IMM8_HI_READ), .out23(decoder_2_out23[23]), .out24(OP_IMM_VAL[0]), .out25(OP_IMM_VAL[1]),
    .out26(OP_IMM_VAL[2]), .out27(OP_IMM_VAL[3]), .out28(OP_IMM_VAL[4]), .out29(OP_IMM_VAL[5]),
    .out30(OP_IMM_VAL[6]), .out31(OP_IMM_VAL[7]), .sel(IROM_VALUE[4:0]), .en(READ_DATA));
  or or_2 (BUS_EXT, PERI0_READ, PERI1_READ, PERI2_READ, DRAM_READ, DROM_READ, PERI0_WRITE, PERI1_WRITE, PERI2_WRITE, DRAM_WRITE);
  stack STACK_X (
    .WRITE_TOS(STACK_X_TOS_WRITE), .READ_TOS(STACK_X_TOS_READ), .RESET(RESET), .DATA_IN(REG_DATA_q),
    .CLK(CLK), .PUSH(STACK_X_PUSH), .POP(STACK_X_POP), .LOAD_SP(STACK_X_SP_WRITE), .SP_IN(REG_DATA_q),
    .DATA_OUT(STACK_X_TOS), .SP_OUT(STACK_X_sp_out));
  stack STACK_Y (
    .WRITE_TOS(STACK_Y_TOS_WRITE), .READ_TOS(STACK_Y_TOS_READ), .RESET(RESET), .DATA_IN(REG_DATA_q),
    .CLK(CLK), .PUSH(STACK_Y_PUSH), .POP(STACK_Y_POP), .LOAD_SP(STACK_Y_SP_WRITE), .SP_IN(REG_DATA_q),
    .DATA_OUT(STACK_XY_TOS), .SP_OUT(STACK_Y_sp_out));
  alu_8 ALU_8BIT (
    .OP(SREG_IMM_21[3:0]), .A(multiplexer_1_out), .B(multiplexer_2_out), .RES(ALU_8BIT_res),
    .CARRY(ALU_8BIT_carry));
  alu_16 ALU_16BIT (.OP(SREG_IMM_21[3:0]), .A(multiplexer_3_out), .B(multiplexer_4_out), .RES(ALU_16BIT_res));
  Register #(.width(16)) register_1 (.D(ALU_16BIT_res), .en(ALU16_LATCH), .clk(CLK), .Q(register_1_q), .clr(RESET));
  assign controlled_buffer_1_out = OP_IMM_READ ? OP_IMM : 8'bz;  // Controlled_Buffer controlled_buffer_3
  assign bit_extender_2_out = {{1{1'b0}}, SREG_IMM7};  // Bit_Extender bit_extender_2
  assign controlled_buffer_1_out = SREG_IMM7_READ ? bit_extender_2_out : 8'bz;  // Controlled_Buffer controlled_buffer_4
  assign controlled_buffer_1_out = SREG_IMM8_LO_READ ? {SREG_IMM8_LO[7], SREG_IMM7} : 8'bz;  // Controlled_Buffer controlled_buffer_5
  assign bit_extender_3_out = {{2{1'b0}}, SREG_IMM8_HI[5:0]};  // Bit_Extender bit_extender_3
  assign controlled_buffer_1_out = SREG_IMM8_HI6_READ ? bit_extender_3_out : 8'bz;  // Controlled_Buffer controlled_buffer_6
  assign controlled_buffer_1_out = SREG_IMM8_HI_READ ? SREG_IMM8_HI : 8'bz;  // Controlled_Buffer controlled_buffer_7
  assign controlled_buffer_1_out = RAM_PAGE_READ ? REG_ADDR_PAGE_q : 8'bz;  // Controlled_Buffer controlled_buffer_8
  assign controlled_buffer_1_out = ROM_PAGE_READ ? ROM_ADDR[23:16] : 8'bz;  // Controlled_Buffer controlled_buffer_9
  assign controlled_buffer_1_out = REGF_A_READ ? REGF_A : 8'bz;  // Controlled_Buffer controlled_buffer_10
  assign controlled_buffer_1_out = REGF_B_READ ? REGF_AB : 8'bz;  // Controlled_Buffer controlled_buffer_11
  assign controlled_buffer_1_out = REGF_I_READ ? REGF_I : 8'bz;  // Controlled_Buffer controlled_buffer_12
  assign controlled_buffer_1_out = REGF_J_READ ? REGF_IJ : 8'bz;  // Controlled_Buffer controlled_buffer_13
  assign controlled_buffer_1_out = STACK_X_TOS_READ ? STACK_X_TOS : 8'bz;  // Controlled_Buffer controlled_buffer_14
  assign controlled_buffer_1_out = STACK_X_SP_READ ? STACK_X_sp_out : 8'bz;  // Controlled_Buffer controlled_buffer_15
  assign controlled_buffer_1_out = STACK_Y_TOS_READ ? STACK_XY_TOS : 8'bz;  // Controlled_Buffer controlled_buffer_16
  assign controlled_buffer_1_out = STACK_Y_SP_READ ? STACK_Y_sp_out : 8'bz;  // Controlled_Buffer controlled_buffer_17
  assign controlled_buffer_1_out = ALU8_RES_READ ? ALU_8BIT_res : 8'bz;  // Controlled_Buffer controlled_buffer_18
  assign controlled_buffer_1_out = ALU8_CARRY_READ ? ALU_8BIT_carry : 8'bz;  // Controlled_Buffer controlled_buffer_19
  assign controlled_buffer_1_out = ALU16_RES_LO_READ ? register_1_q[7:0] : 8'bz;  // Controlled_Buffer controlled_buffer_20
  assign controlled_buffer_1_out = ALU16_RES_HI_READ ? register_1_q[15:8] : 8'bz;  // Controlled_Buffer controlled_buffer_21
  or or_3 (or_3_out, PERI0_WRITE, PERI1_WRITE, PERI2_WRITE, DRAM_WRITE);
  assign DATA_OUT = or_3_out ? controlled_buffer_1_out : 8'bz;  // Controlled_Buffer controlled_buffer_22
  or or_4 (OP_IMM_READ, decoder_2_out23[23], OP_IMM_VAL[0], OP_IMM_VAL[1], OP_IMM_VAL[2], OP_IMM_VAL[3], OP_IMM_VAL[4], OP_IMM_VAL[5], OP_IMM_VAL[6], OP_IMM_VAL[7]);
  and and_3 (SPECIAL_0, ~IROM_VALUE[5], ~IROM_VALUE[6], ~IROM_VALUE[7]);  // AND_Gate
  Decoder #(.select(5)) decoder_3 (
    .out0(HALT), .out1(JUMP), .out2(ALU16_LATCH), .out3(decoder_3_out3[3]), .out4(BRANCH_A_EQZ),
    .out5(BRANCH_A_NEZ), .out6(BRANCH_B_EQZ), .out7(BRANCH_B_NEZ), .out8(STACK_X_PUSH), .out9(STACK_X_POP),
    .out10(STACK_Y_PUSH), .out11(STACK_Y_POP), .out12(decoder_3_out3[12]), .out13(decoder_3_out3[13]),
    .out14(decoder_3_out3[14]), .out15(decoder_3_out3[15]), .out16(decoder_3_out3[16]),
    .out17(decoder_3_out3[17]), .out18(decoder_3_out3[18]), .out19(decoder_3_out3[19]),
    .out20(decoder_3_out3[20]), .out21(decoder_3_out3[21]), .out22(decoder_3_out3[22]),
    .out23(decoder_3_out3[23]), .out24(decoder_3_out3[24]), .out25(decoder_3_out3[25]),
    .out26(decoder_3_out3[26]), .out27(decoder_3_out3[27]), .out28(decoder_3_out3[28]),
    .out29(decoder_3_out3[29]), .out30(decoder_3_out3[30]), .out31(decoder_3_out3[31]),
    .sel(IROM_VALUE[4:0]), .en(SPECIAL_0));
  Comparator #(.mode("unsigned")) comparator_1 (.a(REGF_A), .b({8{1'b0}}), .eq(comparator_1_eq));  // open: gt, lt
  Comparator #(.mode("unsigned")) comparator_2 (.a(REGF_AB), .b({8{1'b0}}), .eq(comparator_2_eq));  // open: gt, lt
  and and_4 (and_4_out, BRANCH_A_EQZ, comparator_1_eq);
  and and_5 (and_5_out, ~comparator_1_eq, BRANCH_A_NEZ);  // AND_Gate
  and and_6 (and_6_out, BRANCH_B_EQZ, comparator_2_eq);
  and and_7 (and_7_out, ~comparator_2_eq, BRANCH_B_NEZ);  // AND_Gate
  or or_5 (or_5_out, INTR, and_4_out, and_5_out, and_6_out, and_7_out, JUMP);
  D_Flip_Flop u_HALT (.D(HALT), .clk(CLK), .Q(HALTED), .Qn(HALT_qn), .reset(RESET));  // open: preset
  Counter #(.max('hffff), .width(16)) CNT_PC (
    .load(or_5_out), .D(LOAD_PC_ADDR), .count(HALT_qn), .Q(ROM_ADDR[15:0]), .clk(CLK), .clr(RESET));  // open: carry, up
  and and_8 (SPECIAL_OP1, IROM_VALUE[5], IROM_VALUE[6], ~IROM_VALUE[7]);  // AND_Gate
  Decoder #(.select(5)) decoder_4 (
    .out0(decoder_4_out0[0]), .out1(decoder_4_out0[1]), .out2(decoder_4_out0[2]), .out3(decoder_4_out0[3]),
    .out4(decoder_4_out0[4]), .out5(decoder_4_out0[5]), .out6(decoder_4_out0[6]), .out7(decoder_4_out0[7]),
    .out8(decoder_4_out0[8]), .out9(decoder_4_out0[9]), .out10(decoder_4_out0[10]),
    .out11(decoder_4_out0[11]), .out12(decoder_4_out0[12]), .out13(decoder_4_out0[13]),
    .out14(decoder_4_out0[14]), .out15(decoder_4_out0[15]), .out16(decoder_4_out0[16]),
    .out17(decoder_4_out0[17]), .out18(decoder_4_out0[18]), .out19(decoder_4_out0[19]),
    .out20(decoder_4_out0[20]), .out21(decoder_4_out0[21]), .out22(decoder_4_out0[22]),
    .out23(decoder_4_out0[23]), .out24(decoder_4_out0[24]), .out25(decoder_4_out0[25]),
    .out26(decoder_4_out0[26]), .out27(decoder_4_out0[27]), .out28(decoder_4_out0[28]),
    .out29(decoder_4_out0[29]), .out30(decoder_4_out0[30]), .out31(decoder_4_out0[31]),
    .sel(IROM_VALUE[4:0]), .en(SPECIAL_OP1));

  // Other names for the same wires on the sheet: RAM_WRITE = DRAM_WRITE; REGF_IJ[7:0] = REGF_I; REGF_J[7:0] = REGF_IJ;
  //   RAM_READ = DRAM_READ; REGF_AB[7:0] = REGF_A; REGF_B[7:0] = REGF_AB; CNT_PC[15:0] = ROM_ADDR[15:0];
  //   SREG_IMM8_LO[6:0] = SREG_IMM7; SREG_IMM14[13:0] = {SREG_IMM8_HI[5:0], SREG_IMM8_LO[7], SREG_IMM7};
  //   SREG_IMM16[15:0] = {SREG_IMM8_HI, SREG_IMM8_LO[7], SREG_IMM7};
  //   SREG_IMM21[15:0] = {SREG_IMM8_HI, SREG_IMM8_LO[7], SREG_IMM7}; SREG_IMM8_HI6[5:0] = SREG_IMM8_HI[5:0];
  //   STACK_XY_TOS[7:0] = STACK_X_TOS; STACK_Y_TOS[7:0] = STACK_XY_TOS
endmodule

module front_panel (
  input  RESET,
  input  CLK,
  input  [2:0] ADDR,
  input  READ,
  input  WRITE,
  input  [7:0] DATA_IN,
  output [7:0] DATA_OUT,
  output INTR
);

  wire CNT_X_carry, CNT_Y_carry, decoder_1_out0, decoder_1_out1, decoder_1_out2, decoder_1_out3,
       decoder_1_out4, decoder_1_out5, decoder_1_out6, decoder_1_out7, decoder_2_out0, decoder_2_out1,
       decoder_2_out2, decoder_2_out3, decoder_2_out4, decoder_2_out5, decoder_2_out6, decoder_2_out7;
  wire [1:0] joystick_1_x, joystick_1_y;
  wire [3:0] button_1_out, REG_GPIO_q, REG_GPIO_q_2;
  wire [6:0] keyboard_1_data;
  wire [7:0] bit_extender_3_out, random_1_out, REG_BUZZ0_q, REG_BUZZ1_q, rgb_video_1_p4, rgb_video_1_p5,
       SREG_LED_MATRIX_p5, SREG_LED_MATRIX_p6, SREG_LED_MATRIX_p7, SREG_LED_MATRIX_p8, SREG_LED_MATRIX_p9,
       SREG_LED_MATRIX_p10, SREG_LED_MATRIX_p11, SREG_LED_MATRIX_p12, SREG_LED_MATRIX_p13,
       SREG_LED_MATRIX_p14, SREG_LED_MATRIX_p15, SREG_LED_MATRIX_p16, undriven, undriven_2, undriven_3,
       undriven_4;
  wire [13:0] bit_extender_1_out, bit_extender_2_out, shifter_1_out, shifter_2_out;

  Decoder #(.select(3)) decoder_1 (
    .out0(decoder_1_out0), .out1(decoder_1_out1), .out2(decoder_1_out2), .out3(decoder_1_out3),
    .out4(decoder_1_out4), .out5(decoder_1_out5), .out6(decoder_1_out6), .out7(decoder_1_out7), .sel(ADDR),
    .en(WRITE));
  Register REG_GPIO (.D(DATA_IN), .en(decoder_1_out0), .clk(CLK), .Q({REG_GPIO_q_2, REG_GPIO_q}), .clr(RESET));
  TTY tty_1 (.data(DATA_IN[6:0]), .clk(CLK), .we(decoder_1_out1), .clr(RESET));
  // RGB_Video #(.height(256), .scale(1), .width(256)) rgb_video_1: pin names not known; wires that end beside it: RESET, CLK, decoder_1_out2, rgb_video_1_p4, rgb_video_1_p5, DATA_IN
  Counter CNT_X (
    .load(decoder_1_out3), .D(DATA_IN), .count(decoder_1_out2), .Q(rgb_video_1_p4), .carry(CNT_X_carry),
    .clk(CLK), .clr(RESET));  // open: up
  Counter CNT_Y (
    .load(decoder_1_out4), .D(DATA_IN), .count(CNT_X_carry), .Q(rgb_video_1_p5), .carry(CNT_Y_carry),
    .clk(CLK), .clr(RESET));  // open: up
  Register REG_BUZZ0 (.D(DATA_IN), .en(decoder_1_out5), .clk(CLK), .Q(REG_BUZZ0_q), .clr(RESET));
  Register REG_BUZZ1 (.D(DATA_IN), .en(decoder_1_out6), .clk(CLK), .Q(REG_BUZZ1_q), .clr(RESET));
  // Shift_Register #(.length(16), .width(8)) SREG_LED_MATRIX: pin names not known; wires that end beside it: RESET, decoder_1_out7, CLK, DATA_IN, SREG_LED_MATRIX_p5, SREG_LED_MATRIX_p6, SREG_LED_MATRIX_p7, SREG_LED_MATRIX_p8, SREG_LED_MATRIX_p9, SREG_LED_MATRIX_p10, SREG_LED_MATRIX_p11, SREG_LED_MATRIX_p12, SREG_LED_MATRIX_p13, SREG_LED_MATRIX_p14, SREG_LED_MATRIX_p15, SREG_LED_MATRIX_p16
  Hex_Digit_Display #(.decimalPoint("false")) hex_digit_display_1 (.value(REG_GPIO_q_2));
  Hex_Digit_Display #(.decimalPoint("false")) hex_digit_display_2 (.value(REG_GPIO_q));
  // RGBLED rgbled_1: pin names not known; wires that end beside it: REG_GPIO_q[1], REG_GPIO_q[0], REG_GPIO_q[2]
  // RGBLED rgbled_2: pin names not known; wires that end beside it: REG_GPIO_q_2[0], REG_GPIO_q[3], REG_GPIO_q_2[1]
  Keyboard keyboard_1 (.clk(CLK), .re(decoder_2_out1), .clr(RESET), .data(keyboard_1_data));  // open: avail
  assign bit_extender_1_out = {{7{1'b0}}, REG_BUZZ0_q[7:1]};  // Bit_Extender bit_extender_1
  assign bit_extender_2_out = {{7{1'b0}}, REG_BUZZ1_q[7:1]};  // Bit_Extender bit_extender_2
  DotMatrix #(.dotshape("circle"), .matrixcols(16), .matrixrows(8)) dotmatrix_1 (
    .col0(undriven), .col1(undriven_2), .col2(undriven_3), .col3(undriven_4), .col4(SREG_LED_MATRIX_p16),
    .col5(SREG_LED_MATRIX_p15), .col6(SREG_LED_MATRIX_p14), .col7(SREG_LED_MATRIX_p13),
    .col8(SREG_LED_MATRIX_p12), .col9(SREG_LED_MATRIX_p11), .col10(SREG_LED_MATRIX_p10),
    .col11(SREG_LED_MATRIX_p9), .col12(SREG_LED_MATRIX_p8), .col13(SREG_LED_MATRIX_p7),
    .col14(SREG_LED_MATRIX_p6), .col15(SREG_LED_MATRIX_p5));
  // LedBar #(.inputtype("row")) ledbar_1: pin names not known; wires that end beside it: {REG_GPIO_q_2, REG_GPIO_q}
  Shifter #(.width(14)) shifter_1 (.in(bit_extender_1_out), .\dist (4'b0011), .out(shifter_1_out));
  Shifter #(.width(14)) shifter_2 (.in(bit_extender_2_out), .\dist (4'b0011), .out(shifter_2_out));
  assign bit_extender_3_out = {{1{1'b0}}, keyboard_1_data};  // Bit_Extender bit_extender_3
  Button button_1 (.out(button_1_out[0]));
  Button button_2 (.out(button_1_out[1]));
  Button button_3 (.out(button_1_out[2]));
  Button button_4 (.out(button_1_out[3]));
  Joystick #(.bits(2)) joystick_1 (.x(joystick_1_x), .y(joystick_1_y));
  // Buzzer #(.channel(1), .vol_width(1), .waveform("Square")) buzzer_1: pin names not known; wires that end beside it: shifter_1_out, REG_BUZZ0_q[0], REG_BUZZ0_q[0]
  // Buzzer #(.channel(2), .vol_width(1), .waveform("Square")) buzzer_2: pin names not known; wires that end beside it: shifter_2_out, REG_BUZZ1_q[0], REG_BUZZ1_q[0]
  or or_1 (INTR, button_1_out[0], button_1_out[1], button_1_out[2], button_1_out[3], CNT_X_carry, CNT_Y_carry, joystick_1_x[0], joystick_1_y[0]);
  Random random_1 (.clr(RESET), .clk(CLK), .out(random_1_out));  // open: next
  assign DATA_OUT = decoder_2_out0 ? {REG_GPIO_q_2, REG_GPIO_q} : 8'bz;  // Controlled_Buffer controlled_buffer_1
  assign DATA_OUT = decoder_2_out1 ? bit_extender_3_out : 8'bz;  // Controlled_Buffer controlled_buffer_2
  assign DATA_OUT = decoder_2_out4 ? {joystick_1_y, joystick_1_x, button_1_out} : 8'bz;  // Controlled_Buffer controlled_buffer_3
  assign DATA_OUT = decoder_2_out2 ? rgb_video_1_p4 : 8'bz;  // Controlled_Buffer controlled_buffer_4
  assign DATA_OUT = decoder_2_out3 ? rgb_video_1_p5 : 8'bz;  // Controlled_Buffer controlled_buffer_5
  assign DATA_OUT = decoder_2_out5 ? random_1_out : 8'bz;  // Controlled_Buffer controlled_buffer_6
  assign DATA_OUT = decoder_2_out6 ? SREG_LED_MATRIX_p5 : 8'bz;  // Controlled_Buffer controlled_buffer_7
  assign DATA_OUT = decoder_2_out7 ? SREG_LED_MATRIX_p6 : 8'bz;  // Controlled_Buffer controlled_buffer_8
  Decoder #(.select(3)) decoder_2 (
    .out0(decoder_2_out0), .out1(decoder_2_out1), .out2(decoder_2_out2), .out3(decoder_2_out3),
    .out4(decoder_2_out4), .out5(decoder_2_out5), .out6(decoder_2_out6), .out7(decoder_2_out7), .sel(ADDR),
    .en(READ));
endmodule

module testbed_mini (
  input  RESET
);

  wire and_1_out, and_2_out, and_3_out, and_4_out, CLK, comparator_1_eq, t3lc_mini_1_ram_read,
       t3lc_mini_1_ram_write;
  wire [2:0] t3lc_mini_1_data_out;
  wire [4:3] t3lc_mini_1_data_out_2;
  wire [7:0] controlled_buffer_1_out, ram_1_dout, rom_1_data, t3lc_mini_1_ram_addr, t3lc_mini_1_rom_addr;
  wire [7:5] t3lc_mini_1_data_out_3;

  Comparator #(.width(5)) comparator_1 (
    .a({t3lc_mini_1_data_out_2, t3lc_mini_1_data_out}), .b({5{1'b0}}), .eq(comparator_1_eq));  // open: gt, lt
  ROM rom_1 (.addr(t3lc_mini_1_rom_addr), .data(rom_1_data));
  RAM ram_1 (
    .addr({t3lc_mini_1_data_out_3, t3lc_mini_1_data_out_2, t3lc_mini_1_data_out}), .we(and_1_out),
    .oe(and_2_out), .clk(CLK), .din(t3lc_mini_1_ram_addr), .dout(ram_1_dout));
  and and_1 (and_1_out, t3lc_mini_1_ram_write, comparator_1_eq);
  and and_2 (and_2_out, comparator_1_eq, t3lc_mini_1_ram_read);
  and and_3 (and_3_out, t3lc_mini_1_ram_write, ~comparator_1_eq);  // AND_Gate
  and and_4 (and_4_out, ~comparator_1_eq, t3lc_mini_1_ram_read);  // AND_Gate
  Clock clock_1 (.out(CLK));
  t3lc_mini t3lc_mini_1 (
    .ROM_VALUE(rom_1_data), .DATA_IN(controlled_buffer_1_out), .CLK(CLK), .RESET(RESET),
    .RAM_WRITE(t3lc_mini_1_ram_write), .RAM_READ(t3lc_mini_1_ram_read),
    .DATA_OUT({t3lc_mini_1_data_out_3, t3lc_mini_1_data_out_2, t3lc_mini_1_data_out}),
    .RAM_ADDR(t3lc_mini_1_ram_addr), .ROM_ADDR(t3lc_mini_1_rom_addr));  // open: HALT
  assign controlled_buffer_1_out = and_2_out ? ram_1_dout : 8'bz;  // Controlled_Buffer controlled_buffer_1
  front_panel front_panel_1 (
    .ADDR(t3lc_mini_1_data_out), .READ(and_4_out), .WRITE(and_3_out), .DATA_IN(t3lc_mini_1_ram_addr),
    .RESET(RESET), .CLK(CLK), .DATA_OUT(controlled_buffer_1_out));  // open: INTR
endmodule

module testbed_medium (
  input  RESET
);

  wire and_1_out, and_2_out, CLK, comparator_1_eq, t3lc_medium_1_ram_read, t3lc_medium_1_ram_write;
  wire [2:0] t3lc_medium_1_ram_addr_2;
  wire [7:0] controlled_buffer_1_out, ram_1_dout, rom_1_data, t3lc_medium_1_data_out;
  wire [12:0] t3lc_medium_1_ram_addr;
  wire [15:0] t3lc_medium_1_rom_addr;

  Comparator #(.width(3)) comparator_1 (
    .a(t3lc_medium_1_ram_addr_2), .b(3'b000), .eq(comparator_1_eq));  // open: gt, lt
  ROM #(.addrWidth(16)) rom_1 (.addr(t3lc_medium_1_rom_addr), .data(rom_1_data));
  RAM #(.addrWidth(13)) ram_1 (
    .addr(t3lc_medium_1_ram_addr), .we(and_1_out), .oe(and_2_out), .clk(CLK), .din(t3lc_medium_1_data_out),
    .dout(ram_1_dout));
  and and_1 (and_1_out, t3lc_medium_1_ram_write, comparator_1_eq);
  and and_2 (and_2_out, comparator_1_eq, t3lc_medium_1_ram_read);
  Clock clock_1 (.out(CLK));
  t3lc_medium t3lc_medium_1 (
    .CLK(CLK), .RESET(RESET), .ROM_VALUE(rom_1_data), .DATA_IN(controlled_buffer_1_out),
    .RAM_READ(t3lc_medium_1_ram_read), .DATA_OUT(t3lc_medium_1_data_out), .ROM_ADDR(t3lc_medium_1_rom_addr),
    .RAM_WRITE(t3lc_medium_1_ram_write), .RAM_ADDR({t3lc_medium_1_ram_addr_2, t3lc_medium_1_ram_addr}));  // open: HALTED
  assign controlled_buffer_1_out = and_2_out ? ram_1_dout : 8'bz;  // Controlled_Buffer controlled_buffer_1
  front_panel front_panel_1 (
    .ADDR(t3lc_medium_1_ram_addr_2), .READ(and_2_out), .WRITE(and_1_out), .DATA_IN(t3lc_medium_1_data_out),
    .RESET(RESET), .CLK(CLK), .DATA_OUT(controlled_buffer_1_out));  // open: INTR
endmodule

module testbed_huge (
  input  RESET
);

  wire CLK, t3lc_huge_1_dram_read, t3lc_huge_1_dram_write, t3lc_huge_1_drom_read, t3lc_huge_1_halted,
       t3lc_huge_1_peri0_read, t3lc_huge_1_peri0_write;
  wire [2:0] t3lc_huge_1_addr;
  wire [7:0] controlled_buffer_1_out, DRAM_dout, DROM_data, IROM_data, t3lc_huge_1_data_out;
  wire [23:0] t3lc_huge_1_rom_addr;
  wire [23:3] t3lc_huge_1_addr_2;

  ROM #(.addrWidth(24)) IROM (.addr(t3lc_huge_1_rom_addr), .data(IROM_data));
  RAM #(.addrWidth(24), .asyncread("true")) DRAM (
    .addr({t3lc_huge_1_addr_2, t3lc_huge_1_addr}), .we(t3lc_huge_1_dram_write), .oe(t3lc_huge_1_dram_read),
    .clk(CLK), .din(t3lc_huge_1_data_out), .dout(DRAM_dout));
  ROM #(.addrWidth(24)) DROM (.addr({t3lc_huge_1_addr_2, t3lc_huge_1_addr}), .data(DROM_data));
  Clock clock_1 (.out(CLK));
  t3lc_huge t3lc_huge_1 (
    .CLK(CLK), .RESET(RESET), .IROM_VALUE(IROM_data), .DATA_IN(controlled_buffer_1_out),
    .DROM_READ(t3lc_huge_1_drom_read), .PERI0_READ(t3lc_huge_1_peri0_read),
    .PERI0_WRITE(t3lc_huge_1_peri0_write), .DRAM_READ(t3lc_huge_1_dram_read),
    .DRAM_WRITE(t3lc_huge_1_dram_write), .DATA_OUT(t3lc_huge_1_data_out), .HALTED(t3lc_huge_1_halted),
    .ADDR({t3lc_huge_1_addr_2, t3lc_huge_1_addr}), .ROM_ADDR(t3lc_huge_1_rom_addr));  // open: INTR, PERI1_READ, PERI1_WRITE, PERI2_READ, PERI2_WRITE
  LED led_1 (.in(t3lc_huge_1_halted));
  assign controlled_buffer_1_out = t3lc_huge_1_dram_read ? DRAM_dout : 8'bz;  // Controlled_Buffer controlled_buffer_1
  assign controlled_buffer_1_out = t3lc_huge_1_drom_read ? DROM_data : 8'bz;  // Controlled_Buffer controlled_buffer_2
  front_panel front_panel_1 (
    .ADDR(t3lc_huge_1_addr), .READ(t3lc_huge_1_peri0_read), .WRITE(t3lc_huge_1_peri0_write),
    .DATA_IN(t3lc_huge_1_data_out), .RESET(RESET), .CLK(CLK), .DATA_OUT(controlled_buffer_1_out));  // open: INTR
endmodule
