// Logisim project t3lc.circ as structural Verilog: 9 circuits, main circuit test_t3lc_mini
module alu (
  input  ENA,
  input  [4:0] OP,
  input  CLK,
  input  RESET,
  input  [7:0] A,
  input  [7:0] B,
  output [7:0] DATA
);

  wire adder_1_cout, comparator_1_eq, comparator_1_gt, decoder_1_out0, decoder_1_out1, decoder_1_out2,
       decoder_1_out3, decoder_1_out4, decoder_1_out5, decoder_1_out6, decoder_1_out7, decoder_1_out8,
       decoder_1_out9, decoder_1_out10, decoder_1_out11, decoder_1_out12, decoder_1_out13, decoder_1_out14,
       decoder_1_out15, or_3_out, subtractor_1_bout;
  wire [7:0] ACC_q, adder_1_out, and_1_out, bit_extender_1_out, bit_extender_2_out, bit_extender_3_out,
       bit_extender_4_out, controlled_buffer_1_out, divider_1_out, divider_1_rem, multiplexer_1_out,
       multiplier_1_cout, multiplier_1_out, negator_1_out, not_1_out, or_1_out, or_2_out, shifter_1_out,
       shifter_2_out, shifter_3_out, shifter_4_out, subtractor_1_out, xor_1_out;

  Adder adder_1 (.a(A), .b(B), .out(adder_1_out), .cin(ACC_q[0]), .cout(adder_1_cout));
  Subtractor subtractor_1 (.a(A), .b(B), .out(subtractor_1_out), .bin(ACC_q[0]), .bout(subtractor_1_bout));
  Multiplier multiplier_1 (.a(A), .b(B), .out(multiplier_1_out), .cin(ACC_q), .cout(multiplier_1_cout));
  Divider divider_1 (.a(A), .b(B), .out(divider_1_out), .upper(ACC_q), .rem(divider_1_rem));
  assign and_1_out = A & B;  // AND_Gate and_1, 8 bits wide
  assign or_1_out = A | B;  // OR_Gate or_1, 8 bits wide
  assign xor_1_out = A ^ B;  // XOR_Gate xor_1, 8 bits wide
  assign not_1_out = ~A;  // NOT_Gate not_1, 8 bits wide
  Shifter shifter_1 (.in(A), .\dist (3'b001), .out(shifter_1_out));
  Shifter shifter_2 (.in(A), .\dist (B[2:0]), .out(shifter_2_out));
  Shifter shifter_3 (.in(A), .\dist (3'b001), .out(shifter_3_out));
  Shifter #(.shift("lr")) shifter_4 (.in(A), .\dist (B[2:0]), .out(shifter_4_out));
  Negator negator_1 (.in(A), .out(negator_1_out));
  Comparator comparator_1 (.a(A), .b(B), .gt(comparator_1_gt), .eq(comparator_1_eq));  // open: lt
  assign bit_extender_1_out = {{7{1'b0}}, adder_1_cout};  // Bit_Extender bit_extender_1
  assign bit_extender_2_out = {{7{1'b0}}, subtractor_1_bout};  // Bit_Extender bit_extender_2
  assign or_2_out = 8'h1 | shifter_3_out;  // OR_Gate or_2, 8 bits wide
  assign bit_extender_3_out = {{7{1'b0}}, comparator_1_gt};  // Bit_Extender bit_extender_3
  assign bit_extender_4_out = {{7{1'b0}}, comparator_1_eq};  // Bit_Extender bit_extender_4
  assign controlled_buffer_1_out = decoder_1_out0 ? bit_extender_1_out : 8'bz;  // Controlled_Buffer controlled_buffer_1
  assign controlled_buffer_1_out = decoder_1_out1 ? bit_extender_2_out : 8'bz;  // Controlled_Buffer controlled_buffer_2
  assign controlled_buffer_1_out = decoder_1_out2 ? multiplier_1_cout : 8'bz;  // Controlled_Buffer controlled_buffer_3
  assign controlled_buffer_1_out = decoder_1_out3 ? divider_1_rem : 8'bz;  // Controlled_Buffer controlled_buffer_4
  Multiplexer #(.width(8)) multiplexer_1 (
    .in0(DATA), .in1(controlled_buffer_1_out), .out(multiplexer_1_out), .sel(or_3_out));
  or or_3 (or_3_out, decoder_1_out0, decoder_1_out1, decoder_1_out2, decoder_1_out3);
  Register ACC (.D(multiplexer_1_out), .en(OP[4]), .clk(CLK), .Q(ACC_q), .clr(RESET));
  Decoder #(.select(4)) decoder_1 (
    .out0(decoder_1_out0), .out1(decoder_1_out1), .out2(decoder_1_out2), .out3(decoder_1_out3),
    .out4(decoder_1_out4), .out5(decoder_1_out5), .out6(decoder_1_out6), .out7(decoder_1_out7),
    .out8(decoder_1_out8), .out9(decoder_1_out9), .out10(decoder_1_out10), .out11(decoder_1_out11),
    .out12(decoder_1_out12), .out13(decoder_1_out13), .out14(decoder_1_out14), .out15(decoder_1_out15),
    .sel(OP[3:0]), .en(ENA));
  assign DATA = decoder_1_out0 ? adder_1_out : 8'bz;  // Controlled_Buffer controlled_buffer_5
  assign DATA = decoder_1_out1 ? subtractor_1_out : 8'bz;  // Controlled_Buffer controlled_buffer_6
  assign DATA = decoder_1_out2 ? multiplier_1_out : 8'bz;  // Controlled_Buffer controlled_buffer_7
  assign DATA = decoder_1_out3 ? divider_1_out : 8'bz;  // Controlled_Buffer controlled_buffer_8
  assign DATA = decoder_1_out4 ? and_1_out : 8'bz;  // Controlled_Buffer controlled_buffer_9
  assign DATA = decoder_1_out5 ? or_1_out : 8'bz;  // Controlled_Buffer controlled_buffer_10
  assign DATA = decoder_1_out6 ? xor_1_out : 8'bz;  // Controlled_Buffer controlled_buffer_11
  assign DATA = decoder_1_out7 ? not_1_out : 8'bz;  // Controlled_Buffer controlled_buffer_12
  assign DATA = decoder_1_out8 ? shifter_1_out : 8'bz;  // Controlled_Buffer controlled_buffer_13
  assign DATA = decoder_1_out9 ? shifter_2_out : 8'bz;  // Controlled_Buffer controlled_buffer_14
  assign DATA = decoder_1_out10 ? or_2_out : 8'bz;  // Controlled_Buffer controlled_buffer_15
  assign DATA = decoder_1_out11 ? shifter_4_out : 8'bz;  // Controlled_Buffer controlled_buffer_16
  assign DATA = decoder_1_out12 ? negator_1_out : 8'bz;  // Controlled_Buffer controlled_buffer_17
  assign DATA = decoder_1_out13 ? bit_extender_3_out : 8'bz;  // Controlled_Buffer controlled_buffer_18
  assign DATA = decoder_1_out14 ? bit_extender_4_out : 8'bz;  // Controlled_Buffer controlled_buffer_19
  assign DATA = decoder_1_out15 ? ACC_q : 8'bz;  // Controlled_Buffer controlled_buffer_20
endmodule

module stack (
  input  [7:0] DATA_IN,
  input  CLK,
  input  RESET,
  input  PUSH,
  input  POP,
  input  WRITE_TOS,
  input  READ_TOS,
  output [7:0] DATA_OUT
);

  wire or_1_out;
  wire [7:0] counter_1_q;

  or or_1 (or_1_out, PUSH, POP);
  Counter counter_1 (.clr(RESET), .up(PUSH), .count(or_1_out), .clk(CLK), .Q(counter_1_q));  // open: load, D, carry
  RAM #(.clearpin("true"), .readbehav("war")) ram_1 (
    .addr(counter_1_q), .we(WRITE_TOS), .oe(READ_TOS), .clk(CLK), .din(DATA_IN), .dout(DATA_OUT), .clr(RESET));
endmodule

module t3lc (
  input  CLK,
  input  RESET,
  input  [7:0] ROM_VALUE,
  input  [7:0] DATA_IN,
  output RAM_READ,
  output RAM_WRITE,
  output [7:0] DATA_OUT,
  output PERI0_WRITE,
  output PERI1_WRITE,
  output HALTED,
  output [15:0] ROM_ADDR,
  output [15:0] RAM_ADDR
);

  wire and_2_out, and_3_out, and_4_out, and_5_out, and_6_out, and_12_out, BRANCH, BRANCH_JUMP,
       comparator_1_eq, decoder_1_out0, decoder_1_out1, decoder_1_out2, decoder_1_out3, decoder_1_out4,
       decoder_1_out5, decoder_2_out0, decoder_2_out1, decoder_2_out2, decoder_2_out3, decoder_2_out5,
       decoder_2_out6, decoder_2_out7, decoder_2_out8, ENA_TARGET, HALT_qn, LAST_IMM_q, LOAD_SP, not_1_out,
       or_1_out, or_3_out, or_4_out, or_5_out, or_6_out, or_7_out, or_8_out, POP, PUSH, RAM_WRITE_t,
       RESET_ALU, TOS;
  wire [4:0] ALU_OP;
  wire [6:5] REG_IMM_q;
  wire [7:0] bit_extender_2_out, CNT_SP_q, controlled_buffer_1_out, controlled_buffer_2_out, decoder_2_out9,
       REG_A_q, REG_B_q, STACK_dout;
  wire [15:0] bit_extender_1_out, BRANCH_ADDR, multiplexer_1_out;

  not not_1 (not_1_out, ROM_VALUE[7]);
  D_Flip_Flop LAST_IMM (.D(ROM_VALUE[7]), .clk(CLK), .Q(LAST_IMM_q), .reset(RESET));  // open: Qn, preset
  Decoder #(.select(3)) decoder_1 (
    .out0(decoder_1_out0), .out1(decoder_1_out1), .out2(decoder_1_out2), .out3(decoder_1_out3),
    .out4(decoder_1_out4), .out5(decoder_1_out5), .out6(LOAD_SP), .out7(RAM_WRITE_t), .sel(ROM_VALUE[6:4]),
    .en(not_1_out));
  and and_1 (RAM_WRITE_t, ROM_VALUE[7], LAST_IMM_q);
  assign controlled_buffer_1_out = and_6_out ? DATA_IN : 8'bz;  // Controlled_Buffer controlled_buffer_1
  and and_2 (and_2_out, decoder_1_out0, ENA_TARGET);
  and and_3 (and_3_out, decoder_1_out1, ENA_TARGET);
  and and_4 (and_4_out, decoder_1_out2, ENA_TARGET);
  and and_5 (and_5_out, decoder_1_out3, ENA_TARGET);
  or or_1 (or_1_out, PUSH, POP);
  assign bit_extender_1_out = {{9{1'b0}}, {REG_IMM_q, ALU_OP}};  // Bit_Extender bit_extender_1
  Register #(.width(7)) REG_IMM (
    .D(ROM_VALUE[6:0]), .en(ROM_VALUE[7]), .clk(CLK), .Q({REG_IMM_q, ALU_OP}), .clr(RESET));
  or or_2 (PUSH, decoder_1_out5, RAM_WRITE_t);
  and and_6 (and_6_out, RAM_WRITE_t, ENA_TARGET);
  Register REG_A (.D(controlled_buffer_1_out), .en(and_2_out), .clk(CLK), .Q(REG_A_q), .clr(RESET));
  Register REG_B (.D(controlled_buffer_1_out), .en(and_3_out), .clk(CLK), .Q(REG_B_q), .clr(RESET));
  Register REG_I (.D(controlled_buffer_1_out), .en(and_4_out), .clk(CLK), .Q(RAM_ADDR[7:0]), .clr(RESET));
  Register REG_J (.D(controlled_buffer_1_out), .en(and_5_out), .clk(CLK), .Q(RAM_ADDR[15:8]), .clr(RESET));
  Counter CNT_SP (
    .load(LOAD_SP), .D(controlled_buffer_1_out), .count(or_1_out), .Q(CNT_SP_q), .up(PUSH), .clk(CLK),
    .clr(RESET));  // open: carry
  Shifter #(.width(16)) shifter_1 (.in(bit_extender_1_out), .\dist (4'b0100), .out(BRANCH_ADDR));
  RAM #(.clearpin("true")) STACK (
    .addr(CNT_SP_q), .we(PUSH), .oe(1'b1), .clk(CLK), .din(controlled_buffer_1_out), .dout(STACK_dout),
    .clr(RESET));
  Decoder #(.select(4)) decoder_2 (
    .out0(decoder_2_out0), .out1(decoder_2_out1), .out2(decoder_2_out2), .out3(decoder_2_out3), .out4(TOS),
    .out5(decoder_2_out5), .out6(decoder_2_out6), .out7(decoder_2_out7), .out8(decoder_2_out8),
    .out9(decoder_2_out9[0]), .out10(decoder_2_out9[1]), .out11(decoder_2_out9[2]),
    .out12(decoder_2_out9[3]), .out13(decoder_2_out9[4]), .out14(decoder_2_out9[5]),
    .out15(decoder_2_out9[7]), .sel(ROM_VALUE[3:0]), .en(not_1_out));
  assign bit_extender_2_out = {{1{1'b0}}, {REG_IMM_q, ALU_OP}};  // Bit_Extender bit_extender_2
  assign controlled_buffer_2_out = decoder_2_out0 ? REG_A_q : 8'bz;  // Controlled_Buffer controlled_buffer_2
  assign controlled_buffer_2_out = decoder_2_out1 ? REG_B_q : 8'bz;  // Controlled_Buffer controlled_buffer_3
  assign controlled_buffer_2_out = decoder_2_out2 ? RAM_ADDR[7:0] : 8'bz;  // Controlled_Buffer controlled_buffer_4
  assign controlled_buffer_2_out = decoder_2_out3 ? RAM_ADDR[15:8] : 8'bz;  // Controlled_Buffer controlled_buffer_5
  or or_3 (or_3_out, decoder_2_out6, RAM_WRITE_t);
  assign controlled_buffer_2_out = or_3_out ? bit_extender_2_out : 8'bz;  // Controlled_Buffer controlled_buffer_6
  assign controlled_buffer_2_out = TOS ? STACK_dout : 8'bz;  // Controlled_Buffer controlled_buffer_7
  and and_7 (RESET_ALU, decoder_2_out1, decoder_1_out1);
  and and_8 (PERI0_WRITE, decoder_2_out2, decoder_1_out2);
  and and_9 (PERI1_WRITE, decoder_2_out3, decoder_1_out3);
  and and_10 (POP, RAM_WRITE_t, decoder_2_out7);
  and and_11 (BRANCH, TOS, decoder_1_out4);
  D_Flip_Flop HALT (.D(and_12_out), .clk(CLK), .Q(HALTED), .Qn(HALT_qn), .reset(RESET));  // open: preset
  and and_12 (and_12_out, decoder_2_out0, decoder_1_out0);
  or or_4 (or_4_out, RESET_ALU, RESET);
  or or_5 (or_5_out, decoder_1_out4, BRANCH_JUMP);
  Multiplexer #(.width(16)) multiplexer_1 (.in0(RAM_ADDR), .in1(BRANCH_ADDR), .out(multiplexer_1_out), .sel(BRANCH));
  Comparator comparator_1 (.a(REG_B_q), .b({8{1'b0}}), .eq(comparator_1_eq));  // open: gt, lt
  or or_6 (or_6_out, decoder_2_out9[0], decoder_2_out9[1], decoder_2_out9[2], decoder_2_out9[3], decoder_2_out9[4], decoder_2_out9[5], decoder_2_out9[7], decoder_2_out8);
  assign controlled_buffer_2_out = or_6_out ? {decoder_2_out9[7], 1'b0, decoder_2_out9[5:0]} : 8'bz;  // Controlled_Buffer controlled_buffer_8
  or or_7 (or_7_out, RESET_ALU, PERI0_WRITE, PERI1_WRITE, POP, BRANCH);
  not not_2 (ENA_TARGET, or_7_out);
  Counter #(.max('hffff), .width(16)) CNT_PC (
    .load(or_5_out), .D(multiplexer_1_out), .count(HALT_qn), .Q(ROM_ADDR), .clk(CLK), .clr(RESET));  // open: carry, up
  and and_13 (BRANCH_JUMP, comparator_1_eq, BRANCH);
  or or_8 (or_8_out, RAM_WRITE_t, PERI0_WRITE, PERI1_WRITE);
  alu alu_1 (
    .ENA(decoder_2_out5), .OP(ALU_OP), .CLK(CLK), .RESET(or_4_out), .A(REG_A_q), .B(REG_B_q),
    .DATA(controlled_buffer_2_out));
  and and_14 (RAM_READ, ENA_TARGET, decoder_2_out7);
  and and_15 (RAM_WRITE, ENA_TARGET, RAM_WRITE_t);
  assign DATA_OUT = or_8_out ? controlled_buffer_2_out : 8'bz;  // Controlled_Buffer controlled_buffer_9

  // Other names for the same wires on the sheet: JUMP_ADDR[15:0] = RAM_ADDR

  // Notes on the sheet:
  //   DATA BUS TARGET
  //   DATA BUS SOURCE
endmodule

module test_t3lc_big (
  input  RESET
);

  wire CLK_out, t3lc_1_peri0_write, t3lc_1_peri1_write, t3lc_1_ram_read, t3lc_1_ram_write;
  wire [7:0] REG_II_q, REG_JJ_q, rom_1_data, t3lc_1_data_out;
  wire [15:0] t3lc_1_ram_addr, t3lc_1_rom_addr;

  Clock CLK (.out(CLK_out));
  t3lc t3lc_1 (
    .CLK(CLK_out), .RESET(RESET), .ROM_VALUE(rom_1_data), .DATA_IN(t3lc_1_data_out), .HALTED(RESET),
    .ROM_ADDR(t3lc_1_rom_addr), .RAM_READ(t3lc_1_ram_read), .RAM_WRITE(t3lc_1_ram_write),
    .DATA_OUT(t3lc_1_data_out), .RAM_ADDR(t3lc_1_ram_addr), .PERI0_WRITE(t3lc_1_peri0_write),
    .PERI1_WRITE(t3lc_1_peri1_write));
  Register REG_II (.D(t3lc_1_data_out), .en(t3lc_1_peri0_write), .clk(CLK_out), .Q(REG_II_q), .clr(RESET));
  Register REG_JJ (.D(t3lc_1_data_out), .en(t3lc_1_peri1_write), .clk(CLK_out), .Q(REG_JJ_q), .clr(RESET));
  RAM #(.addrWidth(21), .clearpin("true"), .databus("bidir")) ram_1 (
    .addr({REG_II_q[6:0], t3lc_1_ram_addr[14:8], t3lc_1_ram_addr[6:0]}), .we(t3lc_1_ram_write),
    .oe(t3lc_1_ram_read), .clk(CLK_out), .data(t3lc_1_data_out), .clr(RESET));
  ROM #(.addrWidth(21)) rom_1 (.addr({REG_JJ_q[6:0], t3lc_1_rom_addr[14:8], t3lc_1_rom_addr[6:0]}), .data(rom_1_data));
endmodule

module test_t3lc_mini (
  input  RESET
);

  wire CLK_out, t3lc_1_halted, t3lc_1_peri0_write, t3lc_1_peri1_write;
  wire [7:0] REG_GPIO_q, rom_1_data, t3lc_1_data_out, t3lc_1_rom_addr;
  wire [15:8] t3lc_1_rom_addr_2;

  Clock CLK (.out(CLK_out));
  ROM rom_1 (.addr(t3lc_1_rom_addr), .data(rom_1_data));
  t3lc t3lc_1 (
    .CLK(CLK_out), .RESET(RESET), .ROM_VALUE(rom_1_data), .DATA_IN(t3lc_1_data_out), .HALTED(t3lc_1_halted),
    .ROM_ADDR({t3lc_1_rom_addr_2, t3lc_1_rom_addr}), .DATA_OUT(t3lc_1_data_out),
    .PERI0_WRITE(t3lc_1_peri0_write), .PERI1_WRITE(t3lc_1_peri1_write));  // open: RAM_READ, RAM_WRITE, RAM_ADDR
  Register REG_GPIO (.D(t3lc_1_data_out), .en(t3lc_1_peri0_write), .clk(CLK_out), .Q(REG_GPIO_q), .clr(RESET));
  LED led_1 (.in(t3lc_1_halted));
  // LedBar #(.inputtype("row")) ledbar_1: pin names not known; wires that end beside it: REG_GPIO_q
  TTY tty_1 (.data(t3lc_1_data_out[6:0]), .clk(CLK_out), .we(t3lc_1_peri1_write), .clr(RESET));
endmodule

module test_t3lc_neumann (
  input  RESET
);

  wire and_1_out, CLK_out, DECODE_out, FETCH_out, t3lc_1_ram_read, t3lc_1_ram_write;
  wire [7:0] controlled_buffer_1_out, OP_q, t3lc_1_data_out;
  wire [15:0] multiplexer_1_out, t3lc_1_ram_addr, t3lc_1_rom_addr;

  Clock CLK (.out(CLK_out));
  Clock #(.highDuration(2), .lowDuration(2)) DECODE (.out(DECODE_out));
  Clock #(.highDuration(2), .lowDuration(2), .phaseOffset(2)) FETCH (.out(FETCH_out));
  and and_1 (and_1_out, FETCH_out, t3lc_1_ram_read);
  assign controlled_buffer_1_out = t3lc_1_ram_write ? t3lc_1_data_out : 8'bz;  // Controlled_Buffer controlled_buffer_1
  t3lc t3lc_1 (
    .CLK(DECODE_out), .RESET(RESET), .ROM_VALUE(OP_q), .DATA_IN(t3lc_1_data_out), .ROM_ADDR(t3lc_1_rom_addr),
    .RAM_READ(t3lc_1_ram_read), .RAM_WRITE(t3lc_1_ram_write), .DATA_OUT(t3lc_1_data_out),
    .RAM_ADDR(t3lc_1_ram_addr));  // open: HALTED, PERI0_WRITE, PERI1_WRITE
  assign t3lc_1_data_out = and_1_out ? controlled_buffer_1_out : 8'bz;  // Controlled_Buffer controlled_buffer_2
  Multiplexer #(.width(16)) multiplexer_1 (
    .in0(t3lc_1_ram_addr), .in1(t3lc_1_rom_addr), .out(multiplexer_1_out), .sel(FETCH_out));
  RAM #(.addrWidth(16), .asyncread("true"), .databus("bidir"), .\type ("nonvolatile")) ram_1 (
    .addr(multiplexer_1_out), .we(t3lc_1_ram_write), .oe(1'b1), .clk(CLK_out), .data(controlled_buffer_1_out));
  Register OP (.D(controlled_buffer_1_out), .en(FETCH_out), .clk(CLK_out), .Q(OP_q), .clr(RESET));
endmodule

module mem_reg (
  input  [6:0] ADDR_IN,
  input  [7:0] DATA_IN,
  input  CLK,
  input  RESET,
  input  WRITE_ADDR,
  input  WRITE_MEM,
  input  READ_MEM,
  output [7:0] DATA_OUT
);

  wire [6:0] register_1_q;

  Register #(.width(7)) register_1 (.D(ADDR_IN), .en(WRITE_ADDR), .clk(CLK), .Q(register_1_q), .clr(RESET));
  RAM #(.addrWidth(7), .clearpin("true"), .readbehav("war")) ram_1 (
    .addr(register_1_q), .we(WRITE_MEM), .oe(READ_MEM), .clk(CLK), .din(DATA_IN), .dout(DATA_OUT), .clr(RESET));
endmodule

module t3lc_mem_reg (
  input  CLK,
  input  RESET,
  input  [7:0] ROM_VALUE,
  input  [7:0] DATA_IN,
  output [7:0] DATA_OUT,
  output HALTED,
  output [15:0] ROM_ADDR,
  output PERI0_WRITE,
  output PERI0_READ,
  output PERI1_WRITE,
  output PERI1_READ,
  output RAM_WRITE,
  output RAM_READ,
  output [15:0] ADDR,
  output [7:0] REG_I_OUT,
  output [7:0] REG_J_OUT
);

  wire ALU_READ, BRANCH, BRANCH_JUMP, comparator_1_eq, decoder_2_out8, HALT, HALT_qn, IMM_PUSH, IMM_READ,
       JUMP, LAST_IMM_q, not_1_out, not_2_out, or_1_out, or_2_out, or_3_out, or_5_out, or_6_out, POP, PUSH,
       REG_I_WRITE, REG_J_WRITE, REGF_A_ADDR_WRITE, REGF_A_MEM_WRITE, REGF_A_READ, REGF_B_ADDR_WRITE,
       REGF_B_MEM_WRITE, REGF_B_READ, RESET_ALU, SPECIAL_OP, STACK_READ, STACK_WRITE;
  wire [6:0] REG_IMM;
  wire [7:0] alu_1_data, bit_extender_1_out, bit_extender_2_out, bit_extender_3_out, bit_extender_4_out,
       decoder_1_out0, decoder_2_out0, decoder_2_out9, multiplexer_1_out, TOS;

  not not_1 (not_1_out, ROM_VALUE[7]);
  Decoder #(.select(3)) decoder_1 (
    .out0(decoder_1_out0[0]), .out1(decoder_1_out0[1]), .out2(decoder_1_out0[2]), .out3(decoder_1_out0[3]),
    .out4(decoder_1_out0[4]), .out5(decoder_1_out0[5]), .out6(decoder_1_out0[6]), .out7(decoder_1_out0[7]),
    .sel(ROM_VALUE[6:4]), .en(not_1_out));
  not not_2 (not_2_out, not_1_out);
  assign {RAM_WRITE, PERI1_WRITE, PERI0_WRITE, REG_J_WRITE, REG_I_WRITE, STACK_WRITE, REGF_B_MEM_WRITE, REGF_A_MEM_WRITE} = decoder_1_out0 & ~bit_extender_1_out;  // AND_Gate and_1, 8 bits wide
  assign bit_extender_1_out = {{7{SPECIAL_OP}}, SPECIAL_OP};  // Bit_Extender bit_extender_1
  Register #(.width(7)) u_REG_IMM (.D(ROM_VALUE[6:0]), .en(not_2_out), .clk(CLK), .Q(REG_IMM), .clr(RESET));
  Register REG_I (.D(DATA_IN), .en(REG_I_WRITE), .clk(CLK), .Q(REG_I_OUT), .clr(RESET));
  Register REG_J (.D(DATA_IN), .en(REG_J_WRITE), .clk(CLK), .Q(REG_J_OUT), .clr(RESET));
  assign bit_extender_2_out = {{1{1'b0}}, REG_IMM};  // Bit_Extender bit_extender_2
  D_Flip_Flop LAST_IMM (.D(not_2_out), .clk(CLK), .Q(LAST_IMM_q), .reset(RESET));  // open: Qn, preset
  Multiplexer #(.width(8)) multiplexer_1 (
    .in0(DATA_IN), .in1(bit_extender_2_out), .out(multiplexer_1_out), .sel(IMM_PUSH));
  or or_1 (or_1_out, PUSH, IMM_PUSH);
  or or_2 (or_2_out, IMM_PUSH, STACK_WRITE);
  and and_2 (IMM_PUSH, not_2_out, LAST_IMM_q);
  mem_reg REGF_A (
    .ADDR_IN(REG_IMM), .DATA_IN(DATA_IN), .CLK(CLK), .RESET(RESET), .WRITE_ADDR(REGF_A_ADDR_WRITE),
    .WRITE_MEM(REGF_A_MEM_WRITE), .READ_MEM(REGF_A_READ), .DATA_OUT(ADDR[7:0]));
  mem_reg REGF_B (
    .ADDR_IN(REG_IMM), .DATA_IN(DATA_IN), .CLK(CLK), .RESET(RESET), .WRITE_ADDR(REGF_B_ADDR_WRITE),
    .WRITE_MEM(REGF_B_MEM_WRITE), .READ_MEM(REGF_B_READ), .DATA_OUT(ADDR[15:8]));
  Decoder #(.select(4)) decoder_2 (
    .out0(decoder_2_out0[0]), .out1(decoder_2_out0[1]), .out2(decoder_2_out0[2]), .out3(decoder_2_out0[3]),
    .out4(decoder_2_out0[4]), .out5(decoder_2_out0[5]), .out6(decoder_2_out0[6]), .out7(decoder_2_out0[7]),
    .out8(decoder_2_out8), .out9(decoder_2_out9[0]), .out10(decoder_2_out9[1]), .out11(decoder_2_out9[2]),
    .out12(decoder_2_out9[3]), .out13(decoder_2_out9[4]), .out14(decoder_2_out9[5]),
    .out15(decoder_2_out9[7]), .sel(ROM_VALUE[3:0]), .en(not_1_out));
  assign bit_extender_3_out = {{7{SPECIAL_OP}}, SPECIAL_OP};  // Bit_Extender bit_extender_3
  or or_3 (or_3_out, RESET_ALU, RESET);
  and and_3 (HALT, decoder_2_out0[0], decoder_1_out0[0]);
  and and_4 (PUSH, decoder_2_out0[1], decoder_1_out0[1]);
  and and_5 (POP, decoder_2_out0[2], decoder_1_out0[2]);
  and and_6 (RESET_ALU, decoder_2_out0[3], decoder_1_out0[3]);
  and and_7 (BRANCH, decoder_2_out0[4], decoder_1_out0[4]);
  and and_8 (JUMP, decoder_2_out0[5], decoder_1_out0[5]);
  and and_9 (REGF_A_ADDR_WRITE, decoder_2_out0[6], decoder_1_out0[6]);
  and and_10 (REGF_B_ADDR_WRITE, decoder_2_out0[7], decoder_1_out0[7]);
  assign {RAM_READ, PERI1_READ, PERI0_READ, ALU_READ, IMM_READ, STACK_READ, REGF_B_READ, REGF_A_READ} = decoder_2_out0 & ~bit_extender_3_out;  // AND_Gate and_11, 8 bits wide
  stack STACK_MEM (
    .CLK(CLK), .RESET(RESET), .PUSH(or_1_out), .POP(POP), .DATA_IN(multiplexer_1_out), .WRITE_TOS(or_2_out),
    .READ_TOS(STACK_READ), .DATA_OUT(TOS));
  or or_4 (SPECIAL_OP, HALT, PUSH, POP, RESET_ALU, BRANCH, JUMP, REGF_A_ADDR_WRITE, REGF_B_ADDR_WRITE);
  and and_12 (BRANCH_JUMP, BRANCH, comparator_1_eq);
  Comparator comparator_1 (.a({8{1'b0}}), .b(TOS), .eq(comparator_1_eq));  // open: gt, lt
  assign bit_extender_4_out = {{1{1'b0}}, REG_IMM};  // Bit_Extender bit_extender_4
  assign DATA_OUT = IMM_READ ? bit_extender_4_out : 8'bz;  // Controlled_Buffer controlled_buffer_1
  assign DATA_OUT = REGF_A_READ ? ADDR[7:0] : 8'bz;  // Controlled_Buffer controlled_buffer_2
  assign DATA_OUT = ALU_READ ? alu_1_data : 8'bz;  // Controlled_Buffer controlled_buffer_3
  alu alu_1 (
    .ENA(ALU_READ), .OP(REG_IMM[4:0]), .CLK(CLK), .RESET(or_3_out), .A(ADDR[7:0]), .B(ADDR[15:8]),
    .DATA(alu_1_data));
  assign DATA_OUT = REGF_B_READ ? ADDR[15:8] : 8'bz;  // Controlled_Buffer controlled_buffer_4
  assign DATA_OUT = STACK_READ ? TOS : 8'bz;  // Controlled_Buffer controlled_buffer_5
  or or_5 (or_5_out, decoder_2_out9[0], decoder_2_out9[1], decoder_2_out9[2], decoder_2_out9[3], decoder_2_out9[4], decoder_2_out9[5], decoder_2_out9[7], decoder_2_out8);
  assign DATA_OUT = or_5_out ? {decoder_2_out9[7], 1'b0, decoder_2_out9[5:0]} : 8'bz;  // Controlled_Buffer controlled_buffer_6
  D_Flip_Flop u_HALT (.D(HALT), .clk(CLK), .Q(HALTED), .Qn(HALT_qn), .reset(RESET));  // open: preset
  or or_6 (or_6_out, JUMP, BRANCH_JUMP);
  Counter #(.max('hffff), .width(16)) CNT_PC (
    .load(or_6_out), .D(ADDR), .count(HALT_qn), .Q(ROM_ADDR), .clk(CLK), .clr(RESET));  // open: carry, up

  // Other names for the same wires on the sheet: REGF_A[7:0] = ADDR[7:0]; REGF_AB[15:0] = ADDR;
  //   REGF_B[7:0] = ADDR[15:8]

  // Notes on the sheet:
  //   DATA BUS TARGET
  //   DATA BUS SOURCE
endmodule

module test_t3lc_mem_reg (
  input  RESET
);

  wire CLK_out, t3lc_mem_reg_1_halted, t3lc_mem_reg_1_ram_read, t3lc_mem_reg_1_ram_write;
  wire [7:0] ram_1_dout, rom_1_data, t3lc_mem_reg_1_data_out;
  wire [15:0] t3lc_mem_reg_1_addr, t3lc_mem_reg_1_rom_addr;

  Clock CLK (.out(CLK_out));
  ROM #(.addrWidth(16)) rom_1 (.addr(t3lc_mem_reg_1_rom_addr), .data(rom_1_data));
  t3lc_mem_reg t3lc_mem_reg_1 (
    .CLK(CLK_out), .RESET(RESET), .ROM_VALUE(rom_1_data), .DATA_IN(t3lc_mem_reg_1_data_out),
    .RAM_READ(t3lc_mem_reg_1_ram_read), .DATA_OUT(t3lc_mem_reg_1_data_out), .HALTED(t3lc_mem_reg_1_halted),
    .ROM_ADDR(t3lc_mem_reg_1_rom_addr), .RAM_WRITE(t3lc_mem_reg_1_ram_write), .ADDR(t3lc_mem_reg_1_addr));  // open: PERI0_READ, PERI1_READ, PERI0_WRITE, PERI1_WRITE, REG_I_OUT, REG_J_OUT
  LED led_1 (.in(t3lc_mem_reg_1_halted));
  RAM #(.addrWidth(16)) ram_1 (
    .addr(t3lc_mem_reg_1_addr), .we(t3lc_mem_reg_1_ram_write), .oe(t3lc_mem_reg_1_ram_read), .clk(CLK_out),
    .din(t3lc_mem_reg_1_data_out), .dout(ram_1_dout));
  assign t3lc_mem_reg_1_data_out = t3lc_mem_reg_1_ram_read ? ram_1_dout : 8'bz;  // Controlled_Buffer controlled_buffer_1
endmodule
