// Digital circuit t3lc.dig as structural Verilog
module t3lc (
  input  CLK,
  input  RESET,
  input  [7:0] ROM_VALUE
);

  wire ALU_READ, driver_1_out, driver_2_out, or_1_out, or_2_out, or_3_out, PERI0_READ, PERI0_WRITE,
       PERI1_READ, PERI1_WRITE, RAM_READ, RAM_WRITE, REG_I_WRITE, REG_IMM_READ, REG_J_WRITE, REGF_A_READ,
       REGF_A_WRITE, REGF_B_READ, REGF_B_WRITE, SPECIAL_OP, STACK_READ, STACK_WRITE;
  wire [6:1] undriven;
  wire [7:0] decoder_2_out_0;
  wire [15:0] decoder_1_out_1;
  wire [15:8] undriven_2;

  Decoder #(.Selector_Bits(4)) decoder_1 (
    .sel(ROM_VALUE[3:0]), .out_0(decoder_1_out_1[0]), .out_1(decoder_1_out_1[1]), .out_2(decoder_1_out_1[2]),
    .out_3(decoder_1_out_1[3]), .out_4(decoder_1_out_1[4]), .out_5(decoder_1_out_1[5]),
    .out_6(decoder_1_out_1[6]), .out_7(decoder_1_out_1[7]), .out_8(decoder_1_out_1[8]),
    .out_9(decoder_1_out_1[9]), .out_10(decoder_1_out_1[10]), .out_11(decoder_1_out_1[11]),
    .out_12(decoder_1_out_1[12]), .out_13(decoder_1_out_1[13]), .out_14(decoder_1_out_1[14]),
    .out_15(decoder_1_out_1[15]));
  Decoder #(.Selector_Bits(3)) decoder_2 (
    .sel(ROM_VALUE[6:4]), .out_0(decoder_2_out_0[0]), .out_1(decoder_2_out_0[1]), .out_2(decoder_2_out_0[2]),
    .out_3(decoder_2_out_0[3]), .out_4(decoder_2_out_0[4]), .out_5(decoder_2_out_0[5]),
    .out_6(decoder_2_out_0[6]), .out_7(decoder_2_out_0[7]));
  assign driver_1_out = ROM_VALUE[7] ? decoder_1_out_1[0] : 1'bz;  // Driver driver_1
  assign driver_2_out = ROM_VALUE[7] ? decoder_2_out_0[0] : 1'bz;  // Driver driver_2
  GraphicCard graphiccard_1 ();  // open: A, str, C, ld, B, D
  assign REGF_A_READ = SPECIAL_OP ? driver_1_out : 1'bz;  // Driver driver_3
  assign REGF_A_WRITE = SPECIAL_OP ? driver_2_out : 1'bz;  // Driver driver_4
  or or_1 (or_1_out, undriven_2[8], undriven_2[9], undriven_2[10], undriven_2[11], undriven_2[12]);
  or or_2 (or_2_out, undriven_2[13], undriven_2[14], undriven_2[15]);
  or or_3 (or_3_out, or_1_out, or_2_out);
  Driver driver_5 (.in(undriven_2[9]), .en(or_3_out));  // open: out
  // Pins of 1 and 7 bits meet at {undriven, ROM_VALUE[7]}
  // Pins of 1 and 16 bits meet at decoder_1_out_1
  // Pins of 1 and 8 bits meet at decoder_2_out_0
  // Pins of 1 and 16 bits meet at {undriven_2, RAM_READ, PERI1_READ, PERI0_READ, ALU_READ, REG_IMM_READ, STACK_READ, REGF_B_READ, REGF_A_READ}
  // Pins of 1 and 8 bits meet at {RAM_WRITE, PERI1_WRITE, PERI0_WRITE, REG_J_WRITE, REG_I_WRITE, STACK_WRITE, REGF_B_WRITE, REGF_A_WRITE}
  // Pins of 1 and 8 bits meet at {undriven_2[15], 1'b0, undriven_2[14:9]}
endmodule
